// Logisim project prodis_v1.2.5_no_raw.circ as structural Verilog: 27 circuits, main circuit main
module main (
);

  wire HWE, LWE, mainclk, output_en, prodis1_1_high_byte, prodis1_1_i_flag, prodis1_1_low_byte,
       prodis1_1_str_data, reset_out, Sys_clk;
  wire [0:0] prodis1_1_inst_adr;
  wire [3:0] IRQ1_out;
  wire [7:0] high_data, high_data_o, low_data, low_data_o;
  wire [14:0] addr, prodis1_1_inst_adr_2;
  wire [15:0] mem_read_ctrl_1_data_o, prodis1_1_mem_data_out, rom_1_data;

  // Text text_1: pin names not known
  // Text text_2: pin names not known
  // Text text_3: pin names not known
  // Text text_4: pin names not known
  // Text text_5: pin names not known
  Button IRQ1 (.out(IRQ1_out[0]));
  Button IRQ2 (.out(IRQ1_out[1]));
  Button IRQ3 (.out(IRQ1_out[2]));
  Button IRQ4 (.out(IRQ1_out[3]));
  LED led_1 (.in(prodis1_1_i_flag));
  Button reset (.out(reset_out));
  Clock #(.highDuration(4), .lowDuration(4)) clk (.out(mainclk));
  Clock sysclk (.out(Sys_clk));
  ROM #(.addrWidth(15), .dataWidth(16)) rom_1 (.addr(prodis1_1_inst_adr_2), .data(rom_1_data));
  prodis1 prodis1_1 (
    .inst_adr({prodis1_1_inst_adr_2, prodis1_1_inst_adr[0]}), .inst_data(rom_1_data), .mem_data_adr(addr),
    .mem_data_in(mem_read_ctrl_1_data_o), .mem_data_out(prodis1_1_mem_data_out), .ldr_data(output_en),
    .str_data(prodis1_1_str_data), .reset(reset_out), .interrupt(IRQ1_out), .clock(mainclk),
    .I_flag(prodis1_1_i_flag), .high_byte(prodis1_1_high_byte), .low_byte(prodis1_1_low_byte));
  Memory_write_ctrl memory_write_ctrl_1 (
    .WE(prodis1_1_str_data), .low_byte(prodis1_1_low_byte), .high_byte(prodis1_1_high_byte),
    .Data_i(prodis1_1_mem_data_out), .LWE(LWE), .HWE(HWE), .Low_data(low_data), .High_data(high_data));
  // Probe on addr
  // Probe on high_data
  RAM #(.addrWidth(15), .databus("bibus")) high (
    .addr(addr), .we(HWE), .oe(1'b1), .clk(Sys_clk), .din(high_data), .dout(high_data_o));
  // Probe on high_data_o
  Mem_Read_Ctrl mem_read_ctrl_1 (
    .high_byte(prodis1_1_high_byte), .low_byte(prodis1_1_low_byte), .low_data(low_data_o),
    .high_data(high_data_o), .OE(output_en), .data_o(mem_read_ctrl_1_data_o));
  // Probe on low_data
  // Probe on mem_read_ctrl_1_data_o
  RAM #(.addrWidth(15), .databus("bibus")) high_2 (
    .addr(addr), .we(LWE), .oe(1'b1), .clk(Sys_clk), .din(low_data), .dout(low_data_o));
  // Probe on low_data_o

  // Notes on the sheet:
  //   PRODIS - Processeur Didactique
  //   HEIG-VD - Institut ReDS
  //   Chef de projet : Michel Starkier
  //   Modifications de Logisim : Yanick Saugy
  //   Développement du processeur : Florent Duployer
  //   Licensed under a Creative Commons License (CC BY-NC-SA 3.0)
  //   Note : Lors d'un changement de logique dans un circuit, les sous-circuits de ce système
  //   se mettent à jour visuelement uniquement si on effectue clic droit sur le sous-système, puis "View <subsystem>".
  //   contents of rom_1 (hex, n*v repeats v):
  //   2020 2104 22ab 2307 240c 2500 1c84 1863 8104 88e1 1f4d e013 20ff 25ff 18*0 4328
endmodule

module prodis1 (
  input  [15:0] mem_data_in,
  input  [15:0] inst_data,
  input  [3:0] interrupt,
  input  reset,
  input  clock,
  output [14:0] mem_data_adr,
  output [15:0] inst_adr,
  output [15:0] mem_data_out,
  output str_data,
  output ldr_data,
  output high_byte,
  output low_byte,
  output I_flag
);

  wire alu_en, branch, decode_1_isalea, decode_1_isalea_branch, decode_en, fetch_1_fetch_en, int_lr_en,
       interrupt_en, mem_en, spsr_irq_en, wrback_en;
  wire [2:0] decode_1_adr_reg_d, decode_1_adr_reg_m, decode_1_adr_reg_mem, decode_1_adr_reg_n, decode_1_imm3,
       reg_bank_control_bus;
  wire [3:0] cpsr, mem_control_bus;
  wire [4:0] decode_1_imm5;
  wire [5:0] fetch_control_bus;
  wire [7:0] decode_1_offset_cond_or_imm8;
  wire [10:0] decode_1_offset_incond;
  wire [15:0] bank_register_1_reg_data_m_out, bank_register_1_reg_data_n_out,
       bank_register_1_reg_mem_data_out, execution_1_data_out, fetch_1_out_13, jump_adr,
       memory_access_1_mem_out, PC_fut, PC_pres;
  wire [21:0] decode_1_execute_control_bus;

  // Text text_1: pin names not known
  // Text text_2: pin names not known
  // Text text_3: pin names not known
  // Text text_4: pin names not known
  // Text text_5: pin names not known
  LED led_1 (.in(fetch_1_fetch_en));
  Fetch fetch_1 (
    .jump_adr(jump_adr), .reset(reset), .out_13(fetch_1_out_13), .inst_data(inst_data), .inst_adr(inst_adr),
    .alu_en(alu_en), .mem_en(mem_en), .wrback_en(wrback_en), .cpsr({I_flag, cpsr}),
    .sel_PC(fetch_control_bus), .fetch_en(fetch_1_fetch_en), .decode_en(decode_en), .IRQ_bus(interrupt),
    .PC_fut(PC_fut), .PC_pres(PC_pres), .clock(clock), .interrupt_en(interrupt_en),
    .spsr_irq_en(spsr_irq_en), .int_lr_en(int_lr_en), .branch(branch), .isalea(decode_1_isalea),
    .isalea_branch(decode_1_isalea_branch));
  // Probe on memory_access_1_mem_out
  // Probe on fetch_1_out_13
  Decode decode_1 (
    .instruction(fetch_1_out_13), .reset(reset), .imm5(decode_1_imm5),
    .offset_incond(decode_1_offset_incond), .offset_cond_or_imm8(decode_1_offset_cond_or_imm8),
    .execute_control_bus(decode_1_execute_control_bus), .mem_control_bus(mem_control_bus),
    .reg_bank_control_bus(reg_bank_control_bus), .fetch_control_bus(fetch_control_bus), .clock(clock),
    .adr_reg_m(decode_1_adr_reg_m), .imm3(decode_1_imm3), .adr_reg_n(decode_1_adr_reg_n),
    .adr_reg_mem(decode_1_adr_reg_mem), .adr_reg_d(decode_1_adr_reg_d), .decode_en(decode_en),
    .alu_en(alu_en), .mem_en(mem_en), .branch(branch), .isalea_branch(decode_1_isalea_branch),
    .isalea(decode_1_isalea));
  LED led_2 (.in(wrback_en));
  LED led_3 (.in(decode_en));
  Bank_Register bank_register_1 (
    .reg_sel_n(decode_1_adr_reg_n), .reg_data_in(memory_access_1_mem_out), .reg_sel_wr(decode_1_adr_reg_d),
    .reg_sel_m(decode_1_adr_reg_m), .reg_data_n_out(bank_register_1_reg_data_n_out),
    .reg_data_m_out(bank_register_1_reg_data_m_out), .reg_sel_mem_data(decode_1_adr_reg_mem),
    .reg_mem_data_out(bank_register_1_reg_mem_data_out), .reset(reset), .wrback_en(wrback_en),
    .br_control_bus(reg_bank_control_bus), .PC_fut(PC_fut), .PC_pres(PC_pres), .clock(clock),
    .interupt_en(interrupt_en), .branch(branch), .jump_adr(jump_adr), .int_lr_en(int_lr_en));
  // Probe on bank_register_1_reg_data_n_out
  // Probe on bank_register_1_reg_data_m_out
  LED led_4 (.in(alu_en));
  Execution execution_1 (
    .reg_data_n_in(bank_register_1_reg_data_n_out), .alu_en(alu_en), .immediate5(decode_1_imm5),
    .reg_data_m_in(bank_register_1_reg_data_m_out), .immediate3(decode_1_imm3),
    .data_out(execution_1_data_out), .reset(reset), .offset_cond_or_immediate8(decode_1_offset_cond_or_imm8),
    .offset_incond(decode_1_offset_incond), .execute_control_bus(decode_1_execute_control_bus),
    .out_15({I_flag, cpsr}), .clock(clock), .interrupt_en(interrupt_en), .spsr_irq_en(spsr_irq_en),
    .jump_adr(jump_adr));
  // Probe on execution_1_data_out
  LED led_5 (.in(mem_en));
  Memory_Access memory_access_1 (
    .data_in(execution_1_data_out), .mem_out(memory_access_1_mem_out), .mem_data_adr(mem_data_adr),
    .mem_data_in(mem_data_in), .mem_en(mem_en), .reset(reset), .mem_control_bus(mem_control_bus),
    .str_data(str_data), .ldr_data(ldr_data), .reg_data_in(bank_register_1_reg_mem_data_out),
    .mem_data_out(mem_data_out), .clock(clock), .High_Byte(high_byte), .Low_Byte(low_byte));

  // Other names for the same wires on the sheet: CLK = clock; cpsr[4] = I_flag; RST = reset

  // Notes on the sheet:
  //   PRODIS1 v1.2 - PIPELINE "ARRET"
  //   Schéma principal de PRODIS1.
  //   les divers signaux de contrôles de PRODIS1.
  //   ainsi qu'un pipeline en 5 niveaux.
  //   même si elles arrivent lors de branch. 
  //   (Voir chronogrammes pour plus de détails.)
  //   Les signaux dans des tunnels (Flèches blanches) représentent
  //   Cette version gèrent les éléments des versions antérieurs,
  //   Si un aléas de type RAW survient, PRODIS1 arrête le pipeline.
  //   Les interruptions fonctionnent également correctement,
  //   Ces signaux contrôlent l'accès en lecture/écriture à la mémoire des données.
  //   WRITE BACK : Retour de la donnée dans la banque des registres
endmodule

module Fetch (
  input  isalea,
  input  isalea_branch,
  input  [15:0] inst_data,
  input  [15:0] PC_pres,
  input  [15:0] jump_adr,
  input  [5:0] sel_PC,
  input  [4:0] cpsr,
  input  branch,
  input  [3:0] IRQ_bus,
  input  reset,
  input  clock,
  output [15:0] inst_adr,
  output [15:0] out_13,
  output [15:0] PC_fut,
  output decode_en,
  output alu_en,
  output mem_en,
  output wrback_en,
  output fetch_en,
  output spsr_irq_en,
  output interrupt_en,
  output int_lr_en
);

  wire and_1_out, and_2_out, and_4_out, and_5_out, and_6_out, decode_lock, gestion_interruption_1_fetch_lock,
       gestion_interruption_1_pre_decode_lock, gestion_interruption_1_raw_lock, not_1_out, not_2_out,
       not_3_out, not_4_out, not_5_out, not_6_out, or_1_out, or_4_out, RAW, register_1_q, register_5_q,
       register_6_q, test_cond_1_test_cond;
  wire [1:1] or_2_out;
  wire [15:0] adder_1_out, interrupt_adr, multiplexer_1_out;

  // Text text_1: pin names not known
  // Text text_2: pin names not known
  // Text text_3: pin names not known
  // Text text_4: pin names not known
  // Text text_5: pin names not known
  Multiplexer #(.width(16), .enable("false")) multiplexer_1 (
    .in0(16'h2), .in1({16{1'b0}}), .out(multiplexer_1_out), .sel(isalea_branch));
  Test_cond test_cond_1 (
    .cond(sel_PC[5:2]), .Z(cpsr[0]), .C(cpsr[2]), .N(cpsr[1]), .V(cpsr[3]),
    .test_cond(test_cond_1_test_cond), .cond_en(sel_PC[1]));
  not not_1 (not_1_out, branch);
  Adder #(.width(16)) adder_1 (.a(PC_pres), .b(multiplexer_1_out), .out(adder_1_out));  // open: cin, cout
  and and_1 (and_1_out, sel_PC[0], not_1_out, test_cond_1_test_cond);
  not not_2 (not_2_out, and_1_out);
  and and_2 (and_2_out, not_2_out, 1'b1);
  not not_3 (not_3_out, branch);
  Register #(.width(1)) register_1 (.D(or_1_out), .en(1'b1), .clk(clock), .Q(register_1_q), .clr(reset));
  or or_1 (or_1_out, and_2_out, not_3_out);
  Multiplexer #(.select(2), .width(16), .enable("false")) multiplexer_2 (
    .in0(adder_1_out), .in1(PC_pres), .in2(jump_adr), .in3(interrupt_adr), .out(PC_fut),
    .sel({or_2_out[1], spsr_irq_en}));
  or or_2 (or_2_out[1], spsr_irq_en, isalea_branch, and_1_out);
  and and_3 (decode_en, register_1_q, ~isalea, not_4_out);  // AND_Gate
  not not_4 (not_4_out, decode_lock);
  Register #(.width(1)) register_2 (.D(decode_en), .en(1'b1), .clk(clock), .Q(alu_en), .clr(reset));
  and and_4 (and_4_out, branch, 1'b1);
  Register #(.width(1)) register_3 (.D(alu_en), .en(1'b1), .clk(clock), .Q(mem_en), .clr(reset));
  Register #(.width(1)) register_4 (.D(mem_en), .en(1'b1), .clk(clock), .Q(wrback_en), .clr(reset));
  and and_5 (and_5_out, not_3_out, not_5_out);
  not not_5 (not_5_out, gestion_interruption_1_fetch_lock);
  or or_3 (fetch_en, and_5_out, and_4_out);
  Gestion_Interruption gestion_interruption_1 (
    .IRQ1(IRQ_bus[0]), .IRQ2(IRQ_bus[1]), .IRQ3(IRQ_bus[2]), .IRQ4(IRQ_bus[3]),
    .interrupt_adr(interrupt_adr), .clock(clock), .reset(reset), .I_flag(cpsr[4]),
    .interrupt_en(interrupt_en), .pre_decode_lock(gestion_interruption_1_pre_decode_lock),
    .int_lr_en(int_lr_en), .fetch_lock(gestion_interruption_1_fetch_lock),
    .raw_lock(gestion_interruption_1_raw_lock), .spsr_irq_en(spsr_irq_en));
  Multiplexer #(.width(16), .enable("false")) multiplexer_3 (
    .in0(inst_data), .in1(16'h46c0), .out(out_13), .sel(isalea));
  Register #(.width(1)) register_5 (
    .D(gestion_interruption_1_pre_decode_lock), .en(1'b1), .clk(clock), .Q(register_5_q), .clr(reset));
  Register #(.width(1)) register_6 (.D(RAW), .en(1'b1), .clk(clock), .Q(register_6_q), .clr(reset));
  or or_4 (or_4_out, register_5_q, gestion_interruption_1_pre_decode_lock);
  and and_6 (and_6_out, gestion_interruption_1_raw_lock, register_6_q);
  not not_6 (not_6_out, and_6_out);
  and and_7 (decode_lock, or_4_out, not_6_out);

  assign inst_adr = PC_pres;

  // Other names for the same wires on the sheet: sel_interrupt_adr = spsr_irq_en; CLK = clock; I_flag = cpsr[4];
  //   RST = reset

  // Notes on the sheet:
  //   FETCH v1.2
  //   d'une instruction de type branch. 
  //   la valeur actuelle du PC, soit en sélectionnant une adresse de saut.
  //   Ce bloc test si la condition requise par l'instruction est correcte.
  //   Cela n'est utile que pour les branch en Thumb code.
  //   Sinon, le fetch et le decode resterait bloqué.
  //   Ce bloc s'occupe d'envoyer la bonne adresse à la mémoire d'instruction, soit en incrémentant
  //   Ce compteur permet de renable le fetch et le decode lorsqu'on arrive à la fin
  //   Le bloc reçoit en retour l'instruction stockée dans la mémoire, qu'il va en ensuite envoyer au bloc suivant : Le décodage.
  //   Incrémentation du PC 
  //   pour que l'instruction se termine correctement.
  //   Si une instruction est decodée, alors les blocs qui suivent sont activés de manière retardées
  //   On sélectionne l'adresse de l'interruption qu'à la fin du compteur de transition.
endmodule

module Test_cond (
  input  cond_en,
  input  [3:0] cond,
  input  Z,
  input  C,
  input  N,
  input  V,
  output test_cond
);

  wire and_1_out, and_2_out, comparator_1_eq, not_1_out, not_2_out, not_3_out, not_4_out, not_5_out,
       not_6_out, not_7_out, not_8_out, or_1_out, or_2_out;
  wire [3:0] multiplexer_1_out;

  // Text text_1: pin names not known
  // Text text_2: pin names not known
  // Text text_3: pin names not known
  // Text text_4: pin names not known
  // Text text_5: pin names not known
  and and_1 (and_1_out, C, not_1_out);
  not not_1 (not_1_out, Z);
  not not_2 (not_2_out, C);
  or or_1 (or_1_out, not_2_out, Z);
  Comparator #(.width(1), .mode("unsigned")) comparator_1 (.a(N), .b(V), .eq(comparator_1_eq));  // open: gt, lt
  not not_3 (not_3_out, Z);
  not not_4 (not_4_out, comparator_1_eq);
  and and_2 (and_2_out, comparator_1_eq, not_3_out);
  or or_2 (or_2_out, not_4_out, Z);
  not not_5 (not_5_out, Z);
  not not_6 (not_6_out, C);
  not not_7 (not_7_out, N);
  not not_8 (not_8_out, V);
  Multiplexer #(.width(4), .enable("false")) multiplexer_1 (
    .in0(4'b1110), .in1(cond), .out(multiplexer_1_out), .sel(cond_en));
  Multiplexer #(.select(4), .enable("false")) multiplexer_2 (
    .in0(Z), .in1(not_5_out), .in2(C), .in3(not_6_out), .in4(N), .in5(not_7_out), .in6(V), .in7(not_8_out),
    .in8(and_1_out), .in9(or_1_out), .in10(comparator_1_eq), .in11(not_4_out), .in12(and_2_out),
    .in13(or_2_out), .in14(1'b1), .in15(1'b1), .out(test_cond), .sel(multiplexer_1_out));

  // Notes on the sheet:
  //   TEST COND v1.0
  //   sélectionnera le bon test.
  //   Ce bloc reçoit les valeurs actuels des flags de conditions, et, suivant l'instruction conditionnelle,
  //   Si l'instruction n'est pas conditionnelle, alors on choisis la "condition" always, qui est toujours à 1.
  //   Always (Inconditionnel)
endmodule

module Gestion_Interruption (
  input  IRQ4,
  input  IRQ3,
  input  IRQ2,
  input  IRQ1,
  input  I_flag,
  input  reset,
  input  clock,
  output interrupt_en,
  output int_lr_en,
  output fetch_lock,
  output pre_decode_lock,
  output raw_lock,
  output [15:0] interrupt_adr,
  output spsr_irq_en
);

  wire comparator_1_eq, comparator_1_gt, comparator_1_lt, comparator_2_eq, comparator_2_gt, comparator_3_lt,
       comparator_5_eq, multiplexer_1_out, multiplexer_2_out, multiplexer_3_out, multiplexer_4_out,
       not_1_out, or_1_out, or_3_out, s_r_ff_1_q, s_r_ff_2_q, s_r_ff_3_q, s_r_ff_4_q;
  wire [1:0] priority_encoder_1_out;
  wire [3:0] counter_1_q;

  // Text text_1: pin names not known
  // Text text_2: pin names not known
  // Text text_3: pin names not known
  // Text text_4: pin names not known
  // Text text_5: pin names not known
  not not_1 (not_1_out, I_flag);
  S_R_Flip_Flop s_r_ff_1 (
    .S(multiplexer_1_out), .R(1'b0), .clk(clock), .Q(s_r_ff_1_q), .reset(or_1_out));  // open: Qn, preset
  Multiplexer #(.enable("false")) multiplexer_1 (
    .in0(s_r_ff_1_q), .in1(IRQ4), .out(multiplexer_1_out), .sel(not_1_out));
  S_R_Flip_Flop s_r_ff_2 (
    .S(multiplexer_2_out), .R(1'b0), .clk(clock), .Q(s_r_ff_2_q), .reset(or_1_out));  // open: Qn, preset
  Multiplexer #(.enable("false")) multiplexer_2 (
    .in0(s_r_ff_2_q), .in1(IRQ3), .out(multiplexer_2_out), .sel(not_1_out));
  S_R_Flip_Flop s_r_ff_3 (
    .S(multiplexer_3_out), .R(1'b0), .clk(clock), .Q(s_r_ff_3_q), .reset(or_1_out));  // open: Qn, preset
  Multiplexer #(.enable("false")) multiplexer_3 (
    .in0(s_r_ff_3_q), .in1(IRQ2), .out(multiplexer_3_out), .sel(not_1_out));
  S_R_Flip_Flop s_r_ff_4 (
    .S(multiplexer_4_out), .R(1'b0), .clk(clock), .Q(s_r_ff_4_q), .reset(or_1_out));  // open: Qn, preset
  Multiplexer #(.enable("false")) multiplexer_4 (
    .in0(s_r_ff_4_q), .in1(IRQ1), .out(multiplexer_4_out), .sel(not_1_out));
  or or_1 (or_1_out, comparator_5_eq, reset);
  Priority_Encoder #(.select(2)) priority_encoder_1 (
    .in0(s_r_ff_1_q), .in1(s_r_ff_2_q), .in2(s_r_ff_3_q), .in3(s_r_ff_4_q), .out(priority_encoder_1_out));  // open: gs, en_out, en_in
  Multiplexer #(.select(2), .width(16), .enable("false")) multiplexer_5 (
    .in0(16'he000), .in1(16'he200), .in2(16'he400), .in3(16'he600), .out(interrupt_adr),
    .sel(priority_encoder_1_out));
  or or_2 (interrupt_en, s_r_ff_1_q, s_r_ff_2_q, s_r_ff_3_q, s_r_ff_4_q);
  or or_3 (or_3_out, comparator_5_eq, reset);
  Counter #(.width(4), .max('hf)) counter_1 (
    .clr(or_3_out), .load(1'b0), .up(1'b1), .count(interrupt_en), .clk(clock), .D(4'b0000), .Q(counter_1_q));  // open: carry
  Comparator #(.width(4), .mode("unsigned")) comparator_1 (
    .a(counter_1_q), .b(4'b0001), .gt(comparator_1_gt), .eq(comparator_1_eq), .lt(comparator_1_lt));
  Comparator #(.width(4), .mode("unsigned")) comparator_2 (
    .a(counter_1_q), .b(4'b0010), .gt(comparator_2_gt), .eq(comparator_2_eq));  // open: lt
  Comparator #(.width(4), .mode("unsigned")) comparator_3 (
    .a(counter_1_q), .b(4'b0101), .lt(comparator_3_lt));  // open: gt, eq
  Comparator #(.width(4), .mode("unsigned")) comparator_4 (
    .a(counter_1_q), .b(4'b0111), .eq(spsr_irq_en));  // open: gt, lt
  Comparator #(.width(4), .mode("unsigned")) comparator_5 (
    .a(counter_1_q), .b(4'b1000), .eq(comparator_5_eq));  // open: gt, lt
  and and_1 (int_lr_en, interrupt_en, comparator_1_lt);
  or or_4 (fetch_lock, comparator_1_gt, comparator_1_eq);
  or or_5 (pre_decode_lock, comparator_2_gt, comparator_2_eq);
  and and_2 (raw_lock, fetch_lock, comparator_3_lt);

  // Other names for the same wires on the sheet: clk = clock; RST = reset

  // Notes on the sheet:
  //   INTERRUPT UNIT v1.2
  //   4 interruptions sont pour l'instant en place. Les sauts vont aux adresses suivantes en fonction de l'IRQ :
  //   Un compteur de 8 coups d'horloges s'enclenche dès qu'on détecte une interruption. Ceci nous permet d'attendre que les
  //   instructions précédentes se terminent correctement, même en cas d'aléas de type RAW, avant qu'on entre dans la routine d'interruption.
  //   IRQ 1 : 0xE000
  //   IRQ 2 : 0xE200
  //   IRQ 3 : 0xE400
  //   IRQ 4 : 0xE600
endmodule

module Bank_Register (
  input  [2:0] reg_sel_n,
  input  clock,
  input  [15:0] reg_data_in,
  input  wrback_en,
  input  [2:0] reg_sel_wr,
  input  [2:0] reg_sel_m,
  input  interupt_en,
  input  branch,
  input  [15:0] jump_adr,
  input  int_lr_en,
  input  [15:0] PC_fut,
  input  [2:0] reg_sel_mem_data,
  input  reset,
  input  [2:0] br_control_bus,
  output [15:0] reg_data_n_out,
  output [15:0] reg_data_m_out,
  output [15:0] reg_mem_data_out,
  output [15:0] PC_pres
);

  wire and_1_out, decoder_1_out0, decoder_1_out1, decoder_1_out2, decoder_1_out3, decoder_1_out4,
       decoder_1_out5, decoder_1_out6, decoder_1_out7, not_1_out, or_1_out, pc_lr_1_lr_en;
  wire [15:0] LR_q, multiplexer_1_out, multiplexer_2_out, multiplexer_3_out, multiplexer_4_out,
       pc_lr_1_lr_in, Reg0_q, Reg1_q, Reg2_q, Reg3_q, Reg4_q, register_1_q, SP_q;

  // Text text_1: pin names not known
  // Text text_2: pin names not known
  // Text text_3: pin names not known
  // Text text_4: pin names not known
  // Text text_5: pin names not known
  and and_1 (and_1_out, br_control_bus[2], wrback_en);
  Decoder #(.select(3)) decoder_1 (
    .out0(decoder_1_out0), .out1(decoder_1_out1), .out2(decoder_1_out2), .out3(decoder_1_out3),
    .out4(decoder_1_out4), .out5(decoder_1_out5), .out6(decoder_1_out6), .out7(decoder_1_out7),
    .sel(reg_sel_wr), .en(and_1_out));
  not not_1 (not_1_out, decoder_1_out7);
  Multiplexer #(.width(16), .enable("false")) multiplexer_1 (
    .in0(reg_data_in), .in1(PC_fut), .out(multiplexer_1_out), .sel(not_1_out));
  or or_1 (or_1_out, decoder_1_out7, interupt_en, 1'b1);
  PC_LR pc_lr_1 (
    .data_in(reg_data_in), .pc(PC_pres), .sel_reg(decoder_1_out6), .interrupt_en(interupt_en),
    .LR_in(pc_lr_1_lr_in), .LR_en(pc_lr_1_lr_en), .branch(branch), .jump_adr(jump_adr), .int_lr_en(int_lr_en));
  Register #(.width(16)) Reg0 (.D(reg_data_in), .en(decoder_1_out0), .clk(clock), .Q(Reg0_q), .clr(reset));
  Register #(.width(16)) Reg1 (.D(reg_data_in), .en(decoder_1_out1), .clk(clock), .Q(Reg1_q), .clr(reset));
  Register #(.width(16)) Reg2 (.D(reg_data_in), .en(decoder_1_out2), .clk(clock), .Q(Reg2_q), .clr(reset));
  Register #(.width(16)) Reg3 (.D(reg_data_in), .en(decoder_1_out3), .clk(clock), .Q(Reg3_q), .clr(reset));
  Register #(.width(16)) Reg4 (.D(reg_data_in), .en(decoder_1_out4), .clk(clock), .Q(Reg4_q), .clr(reset));
  Register #(.width(16)) SP (.D(reg_data_in), .en(decoder_1_out5), .clk(clock), .Q(SP_q), .clr(reset));
  Register #(.width(16)) LR (.D(pc_lr_1_lr_in), .en(pc_lr_1_lr_en), .clk(clock), .Q(LR_q), .clr(reset));
  Register #(.width(16)) PC (.D(multiplexer_1_out), .en(or_1_out), .clk(clock), .Q(PC_pres), .clr(reset));
  Multiplexer #(.select(3), .width(16), .enable("false")) multiplexer_2 (
    .in0(Reg0_q), .in1(Reg1_q), .in2(Reg2_q), .in3(Reg3_q), .in4(Reg4_q), .in5(SP_q), .in6(LR_q),
    .in7(PC_pres), .out(multiplexer_2_out), .sel(reg_sel_n));
  Multiplexer #(.select(3), .width(16), .enable("false")) multiplexer_3 (
    .in0(Reg0_q), .in1(Reg1_q), .in2(Reg2_q), .in3(Reg3_q), .in4(Reg4_q), .in5(SP_q), .in6(LR_q),
    .in7(PC_pres), .out(multiplexer_3_out), .sel(reg_sel_m));
  Multiplexer #(.select(3), .width(16), .enable("false")) multiplexer_4 (
    .in0(Reg0_q), .in1(Reg1_q), .in2(Reg2_q), .in3(Reg3_q), .in4(Reg4_q), .in5(SP_q), .in6(LR_q),
    .in7(PC_pres), .out(multiplexer_4_out), .sel(reg_sel_mem_data));
  Register #(.width(16)) u_Reg_data_n_out (
    .D(multiplexer_2_out), .en(br_control_bus[0]), .clk(clock), .Q(reg_data_n_out), .clr(reset));
  Register #(.width(16)) u_Reg_data_m_out (
    .D(multiplexer_3_out), .en(br_control_bus[0]), .clk(clock), .Q(reg_data_m_out), .clr(reset));
  Register #(.width(16)) register_1 (
    .D(multiplexer_4_out), .en(br_control_bus[1]), .clk(clock), .Q(register_1_q), .clr(reset));
  Register #(.width(16)) u_Reg_mem_data_out (
    .D(register_1_q), .en(1'b1), .clk(clock), .Q(reg_mem_data_out), .clr(reset));

  // Other names for the same wires on the sheet: reg_bank_en = br_control_bus[0]; reg_mem_data_en = br_control_bus[1];
  //   reg_bank_wr = br_control_bus[2]; CLK = clock; RST = reset

  // Notes on the sheet:
  //   BANK REGISTER v1.2
  //   Ce bloc contient les registres de PRODIS1.
  //   2 en tant qu'operand, et 1 une valeur à écrire en mémoire.
  //   L'adresse des registres étant sur 3 bits dans le Thumb Code, 8 registres sont donc disponibles.
  //   Il y a 3 registres en sortie, car certaines instructions peuvent avoir besoin de 3 :
  //   d'où un registre supplémentaire ici.
  //   La donnée "reg_mem_data_out" est une donnée qui va être écrite en mémoire de donnée.
  //   Pour qu'elle arrive en même temps que les autres informations propre au stockage dans le bloc mémoire,
  //   il faut attendre un coup d'horloge supplémentaire pendant que les autres informations s'executent,
endmodule

module PC_LR (
  input  [15:0] data_in,
  input  [15:0] pc,
  input  [15:0] jump_adr,
  input  interrupt_en,
  input  sel_reg,
  input  branch,
  input  int_lr_en,
  output [15:0] LR_in,
  output LR_en
);

  wire or_1_out;
  wire [1:0] priority_encoder_1_out;
  wire [15:0] adder_1_out;

  // Text text_1: pin names not known
  // Text text_2: pin names not known
  // Text text_3: pin names not known
  // Text text_4: pin names not known
  // Text text_5: pin names not known
  Adder #(.width(16)) adder_1 (.a(pc), .b(16'h2), .out(adder_1_out));  // open: cin, cout
  or or_1 (or_1_out, interrupt_en, branch);
  Priority_Encoder #(.select(2)) priority_encoder_1 (
    .in0(1'b1), .in1(interrupt_en), .in3(or_1_out), .out(priority_encoder_1_out));  // open: in2, gs, en_out, en_in
  Multiplexer #(.select(2), .width(16), .enable("false")) multiplexer_1 (
    .in0(data_in), .in1(adder_1_out), .in2(jump_adr), .in3(pc), .out(LR_in), .sel(priority_encoder_1_out));
  or or_2 (LR_en, or_1_out, sel_reg, int_lr_en);

  // Notes on the sheet:
  //   PC to LR v1.2
  //   dans la routine d'interruption.
  //   l'instruction qui suit bloquée dans le fetch.
  //   on va mettre l'adresse du saut du branch dans LR.
  //   Ainsi, au retour de la routine d'interruption, on sautera au saut du branch.
  //   alors LR va prendre la valeur de PC, et non pas de PC + 2.
  //   Ce bloc permet d'écrire la bonne valeur de retour dans LR lors d'un saut en routine d'interruption.
  //   Lors d'une interruptions, on va bloquer le fetch des instructions pendant 8 coups d'horloges.
  //   Ceci permet de terminer les instructions précédentes, même si il y a des aléas.
  //   Si il y a une interruption, sans aléas et sans branch, on va mettre PC + 2 dans LR, et sauter
  //   Si il y a une interruption, et qu il y a un branch qui se termine pendant le temps de transition,
  //   Si l'interruption arrive alors qu'on est déjà dans un aléas (Fetch et decode qui sont disabled),
  //   Ceci s'explique par le fait que l'instruction qui génère l'aléas est bloquée dans le decode, et
  //   L'interruption va terminé l'instruction qui est dans le decode, mais elle ne va pas fetch les instructions qui suivent, ainsi
  //   l'instruction qui est dans le fetch n'est pas executée, on doit donc revenir dessus au retour de l'interruption.
endmodule

module Decode (
  input  [15:0] instruction,
  input  decode_en,
  input  alu_en,
  input  mem_en,
  input  reset,
  input  clock,
  output [2:0] adr_reg_m,
  output [2:0] imm3,
  output [2:0] adr_reg_n,
  output [2:0] adr_reg_mem,
  output [2:0] adr_reg_d,
  output isalea,
  output [2:0] reg_bank_control_bus,
  output branch,
  output [4:0] imm5,
  output isalea_branch,
  output [21:0] execute_control_bus,
  output [10:0] offset_incond,
  output [7:0] offset_cond_or_imm8,
  output [3:0] mem_control_bus,
  output [5:0] fetch_control_bus
);

  wire sel_rm, use_rd, use_reg_mem, use_rm, use_rn;
  wire [1:0] sel_rd, sel_rn;
  wire [2:0] data_splitter_1_rd_2_0, data_splitter_1_rd_or_rn_10_8, data_splitter_1_rm_or_imm3_8_6,
       data_splitter_1_rn_or_rm_5_3, r0_q, r1_q;
  wire [4:0] data_splitter_1_imm5_10_6;
  wire [7:0] data_splitter_1_offset_cond_or_imm8_7_0;
  wire [10:0] data_splitter_1_offset_incond_10_0;

  // Text text_1: pin names not known
  // Text text_2: pin names not known
  // Text text_3: pin names not known
  // Text text_4: pin names not known
  // Text text_5: pin names not known
  Data_Splitter data_splitter_1 (
    .instruction(instruction), .Rm_or_imm3_8_6(data_splitter_1_rm_or_imm3_8_6),
    .Rn_or_Rm_5_3(data_splitter_1_rn_or_rm_5_3), .Rd_2_0(data_splitter_1_rd_2_0),
    .Imm5_10_6(data_splitter_1_imm5_10_6), .offset_incond_10_0(data_splitter_1_offset_incond_10_0),
    .offset_cond_or_imm8_7_0(data_splitter_1_offset_cond_or_imm8_7_0), .cond_11_8(fetch_control_bus[5:2]),
    .Rd_or_Rn_10_8(data_splitter_1_rd_or_rn_10_8));
  Control_Unit control_unit_1 (
    .instruction(instruction), .reset(reset), .sel_op_shift(execute_control_bus[2:0]),
    .sel_mem(mem_control_bus[0]), .sel_rm(sel_rm), .sel_op_alu(execute_control_bus[6:3]),
    .reg_bank_en(reg_bank_control_bus[0]), .sel_operand_2(execute_control_bus[8:7]),
    .str_data(mem_control_bus[1]), .reg_bank_wr(reg_bank_control_bus[2]),
    .reg_mem_data_en(reg_bank_control_bus[1]), .sel_PC(fetch_control_bus[0]),
    .sel_mult_2(execute_control_bus[12:10]), .sel_operand_1(execute_control_bus[9]),
    .flag_en(execute_control_bus[16:13]), .ldr_data(mem_control_bus[2]),
    .sel_carry(execute_control_bus[18:17]), .sel_rn(sel_rn), .sel_shift(execute_control_bus[19]),
    .shift_c_unaffected(execute_control_bus[20]), .sel_cpsr(execute_control_bus[21]), .clock(clock),
    .decode_en(decode_en), .alu_en(alu_en), .mem_en(mem_en), .use_rd(use_rd), .use_rn(use_rn),
    .use_rm(use_rm), .use_reg_mem(use_reg_mem), .branch(branch), .sel_rd(sel_rd),
    .cond_en(fetch_control_bus[1]), .\byte (mem_control_bus[3]));
  Register #(.width(3)) register_1 (
    .D(data_splitter_1_rm_or_imm3_8_6), .en(decode_en), .clk(clock), .Q(imm3), .clr(reset));
  Multiplexer #(.select(2), .width(3), .enable("false")) multiplexer_1 (
    .in0(data_splitter_1_rn_or_rm_5_3), .in1(data_splitter_1_rd_2_0), .in2(data_splitter_1_rd_or_rn_10_8),
    .in3(3'b111), .out(adr_reg_n), .sel(sel_rn));
  Multiplexer #(.select(2), .width(3), .enable("false")) multiplexer_2 (
    .in0(data_splitter_1_rd_2_0), .in1(data_splitter_1_rd_or_rn_10_8), .in2(3'b111), .in3(3'b000),
    .out(adr_reg_mem), .sel(sel_rd));
  Multiplexer #(.width(3), .enable("false")) multiplexer_3 (
    .in0(data_splitter_1_rm_or_imm3_8_6), .in1(data_splitter_1_rn_or_rm_5_3), .out(adr_reg_m), .sel(sel_rm));
  Register #(.width(5)) register_2 (.D(data_splitter_1_imm5_10_6), .en(decode_en), .clk(clock), .Q(imm5), .clr(reset));
  Register #(.width(11)) register_3 (
    .D(data_splitter_1_offset_incond_10_0), .en(decode_en), .clk(clock), .Q(offset_incond), .clr(reset));
  Register register_4 (
    .D(data_splitter_1_offset_cond_or_imm8_7_0), .en(decode_en), .clk(clock), .Q(offset_cond_or_imm8),
    .clr(reset));
  Register #(.width(3)) r0 (.D(adr_reg_mem), .en(1'b1), .clk(clock), .Q(r0_q), .clr(reset));
  Register #(.width(3)) r1 (.D(r0_q), .en(1'b1), .clk(clock), .Q(r1_q), .clr(reset));
  Register #(.width(3)) r2 (.D(r1_q), .en(1'b1), .clk(clock), .Q(adr_reg_d), .clr(reset));
  ALEAS aleas_1 (
    .imm(use_reg_mem), .reg_n(adr_reg_n), .reg_m(adr_reg_m), .r0(r0_q), .INST(instruction), .r1(r1_q),
    .r2(adr_reg_d), .RST(reset), .CLK(clock), .is_alea(isalea));

  assign isalea_branch = branch;

  // Other names for the same wires on the sheet: CLK = clock; cond[3:0] = fetch_control_bus[5:2];
  //   INST[15:0] = instruction; RST = reset

  // Notes on the sheet:
  //   v1.2 :
  //   DECODE v1.2
  //   aux bons timings.
  //   Ajout d'un bloc de gestion des aléas.
  //   Ce bloc permet de décoder l'instruction qu'on reçoit du FETCH.
  //   Il est divisé en 2 sous-blocs : Data Splitter et Control Unit.
  //   Control Unit permet de détecter quelle instruction est entrée et de générer les signaux de contrôles 
  //   Les opérands pour l'execution sont retardée d'un coup d'horloge pour éviter
  //   que les instructions qui suivent ne changent les valeurs des opérands.
  //   Data Splitter s'occupe de récupérer les informations qui peuvent être sortie de l'instruction sans autres traitement.
  //   registre de destination.
  //   Si Rd se trouve aux bits 10 à 8 de l'instruction, c'est qu'il sera utilisé comme opérand et comme 
  //   Les signaux de contrôles ont été regroupé en bus qui sont attribués à chaque bloc.
  //   Rd peut être utilisé comme operand dans le cas de certaines instruction, d'où ce mux.
  //   Cond n'a pas besoin d'être retardé : Les Branch sont des instructions qui bloquent le fetch.
endmodule

module Data_Splitter (
  input  [15:0] instruction,
  output [2:0] Rd_2_0,
  output [2:0] Rn_or_Rm_5_3,
  output [2:0] Rm_or_imm3_8_6,
  output [2:0] Rd_or_Rn_10_8,
  output [4:0] Imm5_10_6,
  output [3:0] cond_11_8,
  output [10:0] offset_incond_10_0,
  output [7:0] offset_cond_or_imm8_7_0
);

  // Text text_1: pin names not known
  // Text text_2: pin names not known
  // Text text_3: pin names not known
  // Text text_4: pin names not known
  // Text text_5: pin names not known

  assign cond_11_8 = instruction[11:8];
  assign Imm5_10_6 = instruction[10:6];
  assign offset_cond_or_imm8_7_0 = instruction[7:0];
  assign offset_incond_10_0 = instruction[10:0];
  assign Rd_2_0 = instruction[2:0];
  assign Rd_or_Rn_10_8 = instruction[10:8];
  assign Rm_or_imm3_8_6 = instruction[8:6];
  assign Rn_or_Rm_5_3 = instruction[5:3];

  // Notes on the sheet:
  //   DATA SPLITTER v1.0
  //   Split les différentes informations disponible dans l'instruction même.
  //   Les 2 numéros à la fin des noms de signaux indiquent leur emplacement dans l'instruction.
endmodule

module Control_Unit (
  input  [15:0] instruction,
  input  decode_en,
  input  alu_en,
  input  mem_en,
  input  clock,
  input  reset,
  output [1:0] sel_rn,
  output [2:0] sel_op_shift,
  output sel_mem,
  output reg_bank_wr,
  output sel_rm,
  output [3:0] sel_op_alu,
  output str_data,
  output [1:0] sel_rd,
  output [1:0] sel_operand_2,
  output ldr_data,
  output cond_en,
  output reg_bank_en,
  output sel_operand_1,
  output [3:0] flag_en,
  output reg_mem_data_en,
  output [2:0] sel_mult_2,
  output use_rd,
  output [1:0] sel_carry,
  output use_rn,
  output sel_shift,
  output use_rm,
  output shift_c_unaffected,
  output sel_cpsr,
  output use_reg_mem,
  output \byte ,
  output branch,
  output sel_PC
);

  wire [15:0] Control_Execute_q, Control_Memory_q, Control_WriteBack_q, decode_control_1_instruction_out,
       execute_control_1_instruction_out, memory_control_1_instruction_out;

  // Text text_1: pin names not known
  // Text text_2: pin names not known
  // Text text_3: pin names not known
  // Text text_4: pin names not known
  // Text text_5: pin names not known
  Decode_Control decode_control_1 (
    .instruction_in(instruction), .instruction_out(decode_control_1_instruction_out), .sel_rn(sel_rn),
    .sel_rm(sel_rm), .reg_bank_en(reg_bank_en), .reg_mem_data_en(reg_mem_data_en), .use_rd(use_rd),
    .sel_rd(sel_rd), .use_rn(use_rn), .branch(branch), .use_reg_mem(use_reg_mem), .use_rm(use_rm));
  Register #(.width(16)) Control_Execute (
    .D(decode_control_1_instruction_out), .en(decode_en), .clk(clock), .Q(Control_Execute_q), .clr(reset));
  Execute_Control execute_control_1 (
    .instruction_in(Control_Execute_q), .instruction_out(execute_control_1_instruction_out),
    .sel_op_shift(sel_op_shift), .sel_op_alu(sel_op_alu), .sel_operand_2(sel_operand_2),
    .sel_operand_1(sel_operand_1), .sel_mult_2(sel_mult_2), .sel_carry(sel_carry), .sel_shift(sel_shift),
    .cond_en(shift_c_unaffected));
  Branch_Control branch_control_1 (.instruction_in(Control_Execute_q), .sel_pc(sel_PC));  // open: out_2, out_3
  Register #(.width(16)) Control_Memory (
    .D(execute_control_1_instruction_out), .en(alu_en), .clk(clock), .Q(Control_Memory_q), .clr(reset));
  Memory_Control memory_control_1 (
    .instruction_in(Control_Memory_q), .instruction_out(memory_control_1_instruction_out), .sel_mem(sel_mem),
    .ldr_data(ldr_data), .str_data(str_data), .flag_z_en(flag_en[0]), .flag_n_en(flag_en[1]),
    .flag_c_en(flag_en[2]), .flag_v_en(flag_en[3]), .sel_cpsr(sel_cpsr), .\byte (\byte ));
  Register #(.width(16)) Control_WriteBack (
    .D(memory_control_1_instruction_out), .en(mem_en), .clk(clock), .Q(Control_WriteBack_q), .clr(reset));
  Writeback_Control writeback_control_1 (
    .instruction_in(Control_WriteBack_q), .reg_bank_wr(reg_bank_wr), .cond_en(cond_en));  // open: sel_PC

  // Other names for the same wires on the sheet: CLK = clock; RST = reset

  // Notes on the sheet:
  //   CONTROL UNIT v1.2
  //   Gère les signaux de contrôle en fonction de l'instruction en cours.
  //   v1.2 : Ajout des enable des différents blocs pour gérer les aléas
  //   Nombreux nouveaux signaux de contrôle du Decode pour gérer les aléas.
  //   L'instruction va elle-même être retardée avec des registres pour générer les signaux aux bons timing dans les blocs de traitement.
  //   Chaque sous-blocs détecte l'instruction en cours et génère la bonne logique aux signaux de contrôles en fonction de cette dernière.
  //   Vérifier si les branch conditionnels fonctionnent avec cette modification
endmodule

module Decode_Opcode (
  input  [15:0] instruction,
  output add_r_r_r,
  output cmn_r_r,
  output bic_r_r,
  output add_r_r_imm,
  output cmp_r_imm,
  output cpy_r_r,
  output cmp_r_r,
  output mov_r_imm,
  output mov_pc,
  output adc_r_r,
  output mul_r_r,
  output add_r_imm,
  output ror_r_r,
  output and_r_r,
  output asr_r_r,
  output tst_r_r,
  output asr_r_r_imm,
  output eor_r_r,
  output bl_msb,
  output lsl_r_r_imm,
  output lsl_r_r,
  output bl_lsb,
  output lsr_r_r_imm,
  output lsr_r_r,
  output bx,
  output sub_r_r_r,
  output mvn_r_r,
  output sub_r_r_imm,
  output neg_r_r,
  output ldrh_r_r_imm,
  output orr_r_r,
  output ldrh_r_r_r,
  output sbc_r_r,
  output strh_r_r_imm,
  output sub_r_imm,
  output strh_r_r_r,
  output ldrb_r_r_imm,
  output b_cond,
  output ldrb_r_r_r,
  output b_incond,
  output strb_r_r_imm,
  output strb_r_r_r
);

  wire and_1_out, comparator_3_eq, comparator_4_eq, comparator_5_eq;

  // Text text_1: pin names not known
  // Text text_2: pin names not known
  // Text text_3: pin names not known
  // Text text_4: pin names not known
  // Text text_5: pin names not known
  Comparator #(.width(7), .mode("unsigned")) comparator_1 (
    .a(instruction[15:9]), .b(7'b0001100), .eq(add_r_r_r));  // open: gt, lt
  Comparator #(.width(7), .mode("unsigned")) comparator_2 (
    .a(instruction[15:9]), .b(7'b0001110), .eq(add_r_r_imm));  // open: gt, lt
  Comparator #(.width(10), .mode("unsigned")) comparator_3 (
    .a(instruction[15:6]), .b(10'h70), .eq(comparator_3_eq));  // open: gt, lt
  and and_1 (and_1_out, comparator_3_eq, comparator_4_eq);
  Comparator #(.width(3), .mode("unsigned")) comparator_4 (
    .a(instruction[2:0]), .b(3'b111), .eq(comparator_4_eq));  // open: gt, lt
  Comparator #(.mode("unsigned")) comparator_5 (
    .a(instruction[15:8]), .b(8'h27), .eq(comparator_5_eq));  // open: gt, lt
  Comparator #(.width(10), .mode("unsigned")) comparator_6 (
    .a(instruction[15:6]), .b(10'h100), .eq(and_r_r));  // open: gt, lt
  Comparator #(.width(5), .mode("unsigned")) comparator_7 (
    .a(instruction[15:11]), .b(5'b00010), .eq(asr_r_r_imm));  // open: gt, lt
  Comparator #(.width(5), .mode("unsigned")) comparator_8 (
    .a(instruction[15:11]), .b({5{1'b0}}), .eq(lsl_r_r_imm));  // open: gt, lt
  Comparator #(.width(5), .mode("unsigned")) comparator_9 (
    .a(instruction[15:11]), .b(5'b00001), .eq(lsr_r_r_imm));  // open: gt, lt
  Comparator #(.width(7), .mode("unsigned")) comparator_10 (
    .a(instruction[15:9]), .b(7'b0001101), .eq(sub_r_r_r));  // open: gt, lt
  Comparator #(.width(7), .mode("unsigned")) comparator_11 (
    .a(instruction[15:9]), .b(7'b0001111), .eq(sub_r_r_imm));  // open: gt, lt
  Comparator #(.width(5), .mode("unsigned")) comparator_12 (
    .a(instruction[15:11]), .b(5'b10001), .eq(ldrh_r_r_imm));  // open: gt, lt
  Comparator #(.width(7), .mode("unsigned")) comparator_13 (
    .a(instruction[15:9]), .b(7'b0101101), .eq(ldrh_r_r_r));  // open: gt, lt
  Comparator #(.width(5), .mode("unsigned")) comparator_14 (
    .a(instruction[15:11]), .b(5'b10000), .eq(strh_r_r_imm));  // open: gt, lt
  Comparator #(.width(7), .mode("unsigned")) comparator_15 (
    .a(instruction[15:9]), .b(7'b0101001), .eq(strh_r_r_r));  // open: gt, lt
  Comparator #(.width(4), .mode("unsigned")) comparator_16 (
    .a(instruction[15:12]), .b(4'b1101), .eq(b_cond));  // open: gt, lt
  Comparator #(.width(5), .mode("unsigned")) comparator_17 (
    .a(instruction[15:11]), .b(5'b11100), .eq(b_incond));  // open: gt, lt
  or or_1 (mov_pc, and_1_out, comparator_5_eq);
  Comparator #(.width(10), .mode("unsigned")) comparator_18 (
    .a(instruction[15:6]), .b(10'h10b), .eq(cmn_r_r));  // open: gt, lt
  Comparator #(.width(5), .mode("unsigned")) comparator_19 (
    .a(instruction[15:11]), .b(5'b00101), .eq(cmp_r_imm));  // open: gt, lt
  Comparator #(.width(10), .mode("unsigned")) comparator_20 (
    .a(instruction[15:6]), .b(10'h10a), .eq(cmp_r_r));  // open: gt, lt
  Comparator #(.width(10), .mode("unsigned")) comparator_21 (
    .a(instruction[15:6]), .b(10'h105), .eq(adc_r_r));  // open: gt, lt
  Comparator #(.width(5), .mode("unsigned")) comparator_22 (
    .a(instruction[15:11]), .b(5'b00110), .eq(add_r_imm));  // open: gt, lt
  Comparator #(.width(10), .mode("unsigned")) comparator_23 (
    .a(instruction[15:6]), .b(10'h104), .eq(asr_r_r));  // open: gt, lt
  Comparator #(.width(10), .mode("unsigned")) comparator_24 (
    .a(instruction[15:6]), .b(10'h101), .eq(eor_r_r));  // open: gt, lt
  Comparator #(.width(10), .mode("unsigned")) comparator_25 (
    .a(instruction[15:6]), .b(10'h102), .eq(lsl_r_r));  // open: gt, lt
  Comparator #(.width(10), .mode("unsigned")) comparator_26 (
    .a(instruction[15:6]), .b(10'h103), .eq(lsr_r_r));  // open: gt, lt
  Comparator #(.width(10), .mode("unsigned")) comparator_27 (
    .a(instruction[15:6]), .b(10'h10f), .eq(mvn_r_r));  // open: gt, lt
  Comparator #(.width(10), .mode("unsigned")) comparator_28 (
    .a(instruction[15:6]), .b(10'h109), .eq(neg_r_r));  // open: gt, lt
  Comparator #(.width(10), .mode("unsigned")) comparator_29 (
    .a(instruction[15:6]), .b(10'h10c), .eq(orr_r_r));  // open: gt, lt
  Comparator #(.width(10), .mode("unsigned")) comparator_30 (
    .a(instruction[15:6]), .b(10'h106), .eq(sbc_r_r));  // open: gt, lt
  Comparator #(.width(5), .mode("unsigned")) comparator_31 (
    .a(instruction[15:11]), .b(5'b00111), .eq(sub_r_imm));  // open: gt, lt
  Comparator #(.width(5), .mode("unsigned")) comparator_32 (
    .a(instruction[15:11]), .b(5'b01111), .eq(ldrb_r_r_imm));  // open: gt, lt
  Comparator #(.width(7), .mode("unsigned")) comparator_33 (
    .a(instruction[15:9]), .b(7'b0101110), .eq(ldrb_r_r_r));  // open: gt, lt
  Comparator #(.width(5), .mode("unsigned")) comparator_34 (
    .a(instruction[15:11]), .b(5'b01110), .eq(strb_r_r_imm));  // open: gt, lt
  Comparator #(.width(7), .mode("unsigned")) comparator_35 (
    .a(instruction[15:9]), .b(7'b0101010), .eq(strb_r_r_r));  // open: gt, lt
  Comparator #(.width(10), .mode("unsigned")) comparator_36 (
    .a(instruction[15:6]), .b(10'h10e), .eq(bic_r_r));  // open: gt, lt
  Comparator #(.width(10), .mode("unsigned")) comparator_37 (
    .a(instruction[15:6]), .b(10'h118), .eq(cpy_r_r));  // open: gt, lt
  Comparator #(.width(5), .mode("unsigned")) comparator_38 (
    .a(instruction[15:11]), .b(5'b00100), .eq(mov_r_imm));  // open: gt, lt
  Comparator #(.width(10), .mode("unsigned")) comparator_39 (
    .a(instruction[15:6]), .b(10'h10d), .eq(mul_r_r));  // open: gt, lt
  Comparator #(.width(10), .mode("unsigned")) comparator_40 (
    .a(instruction[15:6]), .b(10'h107), .eq(ror_r_r));  // open: gt, lt
  Comparator #(.width(10), .mode("unsigned")) comparator_41 (
    .a(instruction[15:6]), .b(10'h108), .eq(tst_r_r));  // open: gt, lt
  Comparator #(.width(5), .mode("unsigned")) comparator_42 (
    .a(instruction[15:11]), .b(5'b11110), .eq(bl_msb));  // open: gt, lt
  Comparator #(.width(5), .mode("unsigned")) comparator_43 (
    .a(instruction[15:11]), .b({5{1'b1}}), .eq(bl_lsb));  // open: gt, lt
  Comparator #(.width(9), .mode("unsigned")) comparator_44 (.a(instruction[15:7]), .b(9'h8e), .eq(bx));  // open: gt, lt

  // Notes on the sheet:
  //   OPCODE DECODER v.1.1
  //   Le signal de la bonne instruction est généré si on la détecte.
  //   Comparaison entre l'instruction et les différentes valeurs possible de celle-ci.
  //   ADD Rd, Rn, Rm
  //   ADD Rd, Rn, #0 to 7
  //   MOV PC, Rm
  //   MOV PC, #0 to 255
  //   AND Rd, Rm
  //   ASR Rd, Rm, #1 to 32
  //   LSL Rd, Rm, #0 to 31
  //   LSR Rd, Rm, #1 to 32
  //   SUB Rd, Rn, Rm
  //   SUB Rd, Rn, #0 to 7
  //   LDRH Rd, [Rn, #0 to 31 * 2]
  //   LDRH Rd, [Rn, Rm]
  //   STRH Rd, [Rn, #0 to 31 * 2]
  //   STRH Rd, [Rn, Rm]
  //   B<cond> <target_address>
  //   B <target_address>
  //   CMN Rd, Rm
  //   CMP Rn, #8
  //   CMP Rn, Rm
  //   ADC Rd, Rm
  //   ADD Rd, #0 to 255
  //   ASR Rd, Rs
  //   EOR Rd, Rm
  //   LSL Rd, Rs
  //   LSR Rd, Rs
  //   MVN Rd, Rm
  //   NEG Rd, Rm
  //   ORR Rd, Rm
  //   SBC Rd, Rm
  //   SUB Rd, #0 to 255
  //   LDRB Rd, [Rn, #0 to 31]
  //   LDRB Rd, [Rn, Rm]
  //   STRB Rd, [Rn, #0 to 31]
  //   STRB Rd, [Rn, Rm]
  //   BIC Rd, Rm
  //   CPY Rd, Rn
  //   MOV Rd, #0 to 255
  //   MUL Rd, Rm
  //   ROR Rd, Rs
  //   TST Rd, Rm
  //   BL 5bits MSB
  //   BL 11bits LSB
  //   BX R6
endmodule

module Decode_Control (
  input  [15:0] instruction_in,
  output [15:0] instruction_out,
  output [1:0] sel_rn,
  output sel_rm,
  output reg_bank_en,
  output reg_mem_data_en,
  output use_rd,
  output [1:0] sel_rd,
  output use_rn,
  output use_rm,
  output branch,
  output use_reg_mem
);

  wire decode_opcode_1_adc_r_r, decode_opcode_1_add_r_imm, decode_opcode_1_add_r_r_imm,
       decode_opcode_1_add_r_r_r, decode_opcode_1_and_r_r, decode_opcode_1_asr_r_r,
       decode_opcode_1_asr_r_r_imm, decode_opcode_1_b_cond, decode_opcode_1_b_incond,
       decode_opcode_1_bic_r_r, decode_opcode_1_bl_lsb, decode_opcode_1_bx, decode_opcode_1_cmn_r_r,
       decode_opcode_1_cmp_r_imm, decode_opcode_1_cmp_r_r, decode_opcode_1_cpy_r_r, decode_opcode_1_eor_r_r,
       decode_opcode_1_ldrb_r_r_imm, decode_opcode_1_ldrb_r_r_r, decode_opcode_1_ldrh_r_r_imm,
       decode_opcode_1_ldrh_r_r_r, decode_opcode_1_lsl_r_r, decode_opcode_1_lsl_r_r_imm,
       decode_opcode_1_lsr_r_r, decode_opcode_1_lsr_r_r_imm, decode_opcode_1_mov_pc,
       decode_opcode_1_mov_r_imm, decode_opcode_1_mul_r_r, decode_opcode_1_mvn_r_r, decode_opcode_1_neg_r_r,
       decode_opcode_1_orr_r_r, decode_opcode_1_ror_r_r, decode_opcode_1_sbc_r_r,
       decode_opcode_1_strb_r_r_imm, decode_opcode_1_strb_r_r_r, decode_opcode_1_strh_r_r_imm,
       decode_opcode_1_strh_r_r_r, decode_opcode_1_sub_r_imm, decode_opcode_1_sub_r_r_imm,
       decode_opcode_1_sub_r_r_r, decode_opcode_1_tst_r_r, or_3_out, or_4_out, or_5_out, reg_bank_en_2_out,
       reg_bank_en_out, use_rd_out;

  // Text text_1: pin names not known
  // Text text_2: pin names not known
  // Text text_3: pin names not known
  // Text text_4: pin names not known
  // Text text_5: pin names not known
  Decode_Opcode decode_opcode_1 (
    .instruction(instruction_in), .add_r_r_r(decode_opcode_1_add_r_r_r),
    .add_r_r_imm(decode_opcode_1_add_r_r_imm), .and_r_r(decode_opcode_1_and_r_r),
    .asr_r_r_imm(decode_opcode_1_asr_r_r_imm), .lsl_r_r_imm(decode_opcode_1_lsl_r_r_imm),
    .lsr_r_r_imm(decode_opcode_1_lsr_r_r_imm), .sub_r_r_r(decode_opcode_1_sub_r_r_r),
    .sub_r_r_imm(decode_opcode_1_sub_r_r_imm), .ldrh_r_r_imm(decode_opcode_1_ldrh_r_r_imm),
    .ldrh_r_r_r(decode_opcode_1_ldrh_r_r_r), .strh_r_r_imm(decode_opcode_1_strh_r_r_imm),
    .strh_r_r_r(decode_opcode_1_strh_r_r_r), .b_cond(decode_opcode_1_b_cond),
    .b_incond(decode_opcode_1_b_incond), .adc_r_r(decode_opcode_1_adc_r_r),
    .cmn_r_r(decode_opcode_1_cmn_r_r), .cmp_r_imm(decode_opcode_1_cmp_r_imm),
    .cmp_r_r(decode_opcode_1_cmp_r_r), .add_r_imm(decode_opcode_1_add_r_imm),
    .asr_r_r(decode_opcode_1_asr_r_r), .eor_r_r(decode_opcode_1_eor_r_r), .lsl_r_r(decode_opcode_1_lsl_r_r),
    .lsr_r_r(decode_opcode_1_lsr_r_r), .mvn_r_r(decode_opcode_1_mvn_r_r), .neg_r_r(decode_opcode_1_neg_r_r),
    .orr_r_r(decode_opcode_1_orr_r_r), .sbc_r_r(decode_opcode_1_sbc_r_r),
    .sub_r_imm(decode_opcode_1_sub_r_imm), .ldrb_r_r_imm(decode_opcode_1_ldrb_r_r_imm),
    .strb_r_r_imm(decode_opcode_1_strb_r_r_imm), .ldrb_r_r_r(decode_opcode_1_ldrb_r_r_r),
    .strb_r_r_r(decode_opcode_1_strb_r_r_r), .bic_r_r(decode_opcode_1_bic_r_r),
    .cpy_r_r(decode_opcode_1_cpy_r_r), .mov_r_imm(decode_opcode_1_mov_r_imm),
    .mul_r_r(decode_opcode_1_mul_r_r), .ror_r_r(decode_opcode_1_ror_r_r), .tst_r_r(decode_opcode_1_tst_r_r),
    .bl_msb(sel_rd[1]), .bl_lsb(decode_opcode_1_bl_lsb), .bx(decode_opcode_1_bx),
    .mov_pc(decode_opcode_1_mov_pc));
  or bit1 (sel_rn[1], decode_opcode_1_b_cond, decode_opcode_1_b_incond, decode_opcode_1_cmp_r_imm, decode_opcode_1_add_r_imm, decode_opcode_1_sub_r_imm, decode_opcode_1_mov_r_imm, decode_opcode_1_bl_lsb);
  or bit0 (sel_rn[0], decode_opcode_1_and_r_r, decode_opcode_1_b_cond, decode_opcode_1_b_incond, decode_opcode_1_cmn_r_r, decode_opcode_1_cmp_r_r, decode_opcode_1_adc_r_r, decode_opcode_1_asr_r_r, decode_opcode_1_eor_r_r, decode_opcode_1_lsl_r_r, decode_opcode_1_lsr_r_r, decode_opcode_1_orr_r_r, decode_opcode_1_sbc_r_r, decode_opcode_1_bic_r_r, decode_opcode_1_mul_r_r, decode_opcode_1_ror_r_r, decode_opcode_1_tst_r_r, decode_opcode_1_bl_lsb);
  or bit0_2 (sel_rd[0], decode_opcode_1_b_cond, decode_opcode_1_b_incond, decode_opcode_1_cmp_r_r, decode_opcode_1_add_r_imm, decode_opcode_1_sub_r_imm, decode_opcode_1_mov_r_imm, decode_opcode_1_bl_lsb);
  or u_sel_rm (sel_rm, decode_opcode_1_and_r_r, decode_opcode_1_cmn_r_r, decode_opcode_1_cmp_r_r, decode_opcode_1_adc_r_r, decode_opcode_1_asr_r_r, decode_opcode_1_eor_r_r, decode_opcode_1_lsl_r_r, decode_opcode_1_lsr_r_r, decode_opcode_1_neg_r_r, decode_opcode_1_orr_r_r, decode_opcode_1_sbc_r_r, decode_opcode_1_bic_r_r, decode_opcode_1_cpy_r_r, decode_opcode_1_mul_r_r, decode_opcode_1_ror_r_r, decode_opcode_1_tst_r_r);
  or u_reg_bank_en (reg_bank_en_out, decode_opcode_1_add_r_r_r, decode_opcode_1_add_r_r_imm, decode_opcode_1_and_r_r, decode_opcode_1_asr_r_r_imm, decode_opcode_1_lsl_r_r_imm, decode_opcode_1_lsr_r_r_imm, decode_opcode_1_sub_r_r_r, decode_opcode_1_sub_r_r_imm, decode_opcode_1_ldrh_r_r_imm, decode_opcode_1_ldrh_r_r_r, decode_opcode_1_strh_r_r_imm, decode_opcode_1_strh_r_r_r, decode_opcode_1_b_cond, decode_opcode_1_b_incond, decode_opcode_1_cmn_r_r, decode_opcode_1_cmp_r_imm, decode_opcode_1_cmp_r_r, decode_opcode_1_adc_r_r, decode_opcode_1_add_r_imm, decode_opcode_1_asr_r_r);
  or or_1 (reg_bank_en, reg_bank_en_out, reg_bank_en_2_out);
  or reg_bank_en_2 (reg_bank_en_2_out, decode_opcode_1_eor_r_r, decode_opcode_1_lsl_r_r, decode_opcode_1_lsr_r_r, decode_opcode_1_mvn_r_r, decode_opcode_1_neg_r_r, decode_opcode_1_orr_r_r, decode_opcode_1_sbc_r_r, decode_opcode_1_sub_r_imm, decode_opcode_1_ldrb_r_r_imm, decode_opcode_1_ldrb_r_r_r, decode_opcode_1_strb_r_r_imm, decode_opcode_1_strb_r_r_r, decode_opcode_1_bic_r_r, decode_opcode_1_cpy_r_r, decode_opcode_1_mov_r_imm, decode_opcode_1_mul_r_r, decode_opcode_1_ror_r_r, decode_opcode_1_tst_r_r, sel_rd[1], decode_opcode_1_bl_lsb, decode_opcode_1_bx);
  or u_reg_mem_data_en (reg_mem_data_en, decode_opcode_1_strh_r_r_imm, decode_opcode_1_strh_r_r_r, decode_opcode_1_strb_r_r_imm, decode_opcode_1_strb_r_r_r);
  or u_use_rd (use_rd_out, decode_opcode_1_add_r_r_r, decode_opcode_1_add_r_r_imm, decode_opcode_1_and_r_r, decode_opcode_1_asr_r_r_imm, decode_opcode_1_lsl_r_r_imm, decode_opcode_1_lsr_r_r_imm, decode_opcode_1_sub_r_r_r, decode_opcode_1_sub_r_r_imm, decode_opcode_1_ldrh_r_r_imm, decode_opcode_1_ldrh_r_r_r, 1'b0, decode_opcode_1_strh_r_r_r, decode_opcode_1_adc_r_r, decode_opcode_1_add_r_imm, decode_opcode_1_asr_r_r, decode_opcode_1_eor_r_r, decode_opcode_1_lsl_r_r, decode_opcode_1_lsr_r_r, decode_opcode_1_mvn_r_r, decode_opcode_1_neg_r_r, decode_opcode_1_orr_r_r, decode_opcode_1_sbc_r_r, decode_opcode_1_sub_r_imm, decode_opcode_1_ldrb_r_r_imm, decode_opcode_1_ldrb_r_r_r, decode_opcode_1_strb_r_r_imm, decode_opcode_1_strb_r_r_r, decode_opcode_1_bic_r_r, decode_opcode_1_cpy_r_r, decode_opcode_1_mov_r_imm, decode_opcode_1_mul_r_r, decode_opcode_1_ror_r_r);
  or or_2 (use_rd, use_rd_out, or_3_out);
  buf or_3 (or_3_out, sel_rd[1]);  // OR_Gate
  or or_4 (or_4_out, decode_opcode_1_add_r_r_r, decode_opcode_1_add_r_r_imm, decode_opcode_1_and_r_r, decode_opcode_1_asr_r_r_imm, decode_opcode_1_lsl_r_r_imm, decode_opcode_1_lsr_r_r_imm, decode_opcode_1_sub_r_r_r, decode_opcode_1_sub_r_r_imm, decode_opcode_1_ldrh_r_r_imm, decode_opcode_1_ldrh_r_r_r, decode_opcode_1_strh_r_r_imm, decode_opcode_1_strh_r_r_r, decode_opcode_1_cmn_r_r, decode_opcode_1_cmp_r_imm, decode_opcode_1_cmp_r_r, decode_opcode_1_adc_r_r, decode_opcode_1_add_r_imm, decode_opcode_1_asr_r_r, decode_opcode_1_eor_r_r, decode_opcode_1_lsl_r_r, decode_opcode_1_lsr_r_r, decode_opcode_1_mvn_r_r, decode_opcode_1_orr_r_r, decode_opcode_1_sbc_r_r, decode_opcode_1_sub_r_imm, decode_opcode_1_ldrb_r_r_imm, decode_opcode_1_ldrb_r_r_r, decode_opcode_1_strb_r_r_imm, decode_opcode_1_strb_r_r_r, decode_opcode_1_bic_r_r, decode_opcode_1_cpy_r_r);
  or u_use_rn (use_rn, or_4_out, or_5_out);
  or or_5 (or_5_out, decode_opcode_1_mul_r_r, decode_opcode_1_ror_r_r, decode_opcode_1_tst_r_r, decode_opcode_1_bl_lsb);
  or u_use_rm (use_rm, decode_opcode_1_add_r_r_r, decode_opcode_1_and_r_r, decode_opcode_1_sub_r_r_r, 1'b0, decode_opcode_1_ldrh_r_r_r, decode_opcode_1_strh_r_r_r, decode_opcode_1_cmn_r_r, decode_opcode_1_cmp_r_r, decode_opcode_1_adc_r_r, decode_opcode_1_asr_r_r, decode_opcode_1_eor_r_r, decode_opcode_1_lsl_r_r, decode_opcode_1_lsr_r_r, decode_opcode_1_neg_r_r, decode_opcode_1_orr_r_r, decode_opcode_1_sbc_r_r, decode_opcode_1_ldrb_r_r_r, decode_opcode_1_strb_r_r_r, decode_opcode_1_bic_r_r, decode_opcode_1_cpy_r_r, decode_opcode_1_mul_r_r, decode_opcode_1_ror_r_r, decode_opcode_1_tst_r_r);
  or u_branch (branch, decode_opcode_1_b_cond, decode_opcode_1_b_incond, decode_opcode_1_bl_lsb, decode_opcode_1_bx, decode_opcode_1_mov_pc);
  or u_use_reg_mem (use_reg_mem, decode_opcode_1_strh_r_r_imm, decode_opcode_1_strh_r_r_r, decode_opcode_1_strb_r_r_imm, decode_opcode_1_strb_r_r_r);

  assign instruction_out = instruction_in;

  // Notes on the sheet:
  //   Modif: prodis1.2.2. KGS
  //   Modif: prodis 1.2.2 KGS 01/05/2015
endmodule

module Execute_Control (
  input  [15:0] instruction_in,
  output [15:0] instruction_out,
  output [2:0] sel_op_shift,
  output sel_shift,
  output [3:0] sel_op_alu,
  output sel_operand_1,
  output [1:0] sel_operand_2,
  output [2:0] sel_mult_2,
  output [1:0] sel_carry,
  output cond_en
);

  wire decode_opcode_1_add_r_imm, decode_opcode_1_add_r_r_imm, decode_opcode_1_add_r_r_r,
       decode_opcode_1_and_r_r, decode_opcode_1_asr_r_r, decode_opcode_1_asr_r_r_imm, decode_opcode_1_b_cond,
       decode_opcode_1_b_incond, decode_opcode_1_bic_r_r, decode_opcode_1_bl_lsb, decode_opcode_1_bl_msb,
       decode_opcode_1_cmn_r_r, decode_opcode_1_cmp_r_imm, decode_opcode_1_cmp_r_r, decode_opcode_1_cpy_r_r,
       decode_opcode_1_eor_r_r, decode_opcode_1_ldrb_r_r_imm, decode_opcode_1_ldrb_r_r_r,
       decode_opcode_1_ldrh_r_r_imm, decode_opcode_1_ldrh_r_r_r, decode_opcode_1_lsl_r_r,
       decode_opcode_1_lsl_r_r_imm, decode_opcode_1_lsr_r_r, decode_opcode_1_lsr_r_r_imm,
       decode_opcode_1_mov_r_imm, decode_opcode_1_mvn_r_r, decode_opcode_1_neg_r_r, decode_opcode_1_orr_r_r,
       decode_opcode_1_strb_r_r_imm, decode_opcode_1_strb_r_r_r, decode_opcode_1_strh_r_r_imm,
       decode_opcode_1_strh_r_r_r, decode_opcode_1_sub_r_imm, decode_opcode_1_sub_r_r_imm,
       decode_opcode_1_sub_r_r_r, decode_opcode_1_tst_r_r;

  // Text text_1: pin names not known
  // Text text_2: pin names not known
  // Text text_3: pin names not known
  // Text text_4: pin names not known
  // Text text_5: pin names not known
  Decode_Opcode decode_opcode_1 (
    .instruction(instruction_in), .add_r_r_r(decode_opcode_1_add_r_r_r),
    .add_r_r_imm(decode_opcode_1_add_r_r_imm), .and_r_r(decode_opcode_1_and_r_r),
    .asr_r_r_imm(decode_opcode_1_asr_r_r_imm), .lsl_r_r_imm(decode_opcode_1_lsl_r_r_imm),
    .lsr_r_r_imm(decode_opcode_1_lsr_r_r_imm), .sub_r_r_r(decode_opcode_1_sub_r_r_r),
    .sub_r_r_imm(decode_opcode_1_sub_r_r_imm), .ldrh_r_r_imm(decode_opcode_1_ldrh_r_r_imm),
    .ldrh_r_r_r(decode_opcode_1_ldrh_r_r_r), .strh_r_r_imm(decode_opcode_1_strh_r_r_imm),
    .strh_r_r_r(decode_opcode_1_strh_r_r_r), .b_cond(decode_opcode_1_b_cond),
    .b_incond(decode_opcode_1_b_incond), .adc_r_r(sel_carry[0]), .cmn_r_r(decode_opcode_1_cmn_r_r),
    .cmp_r_imm(decode_opcode_1_cmp_r_imm), .cmp_r_r(decode_opcode_1_cmp_r_r),
    .add_r_imm(decode_opcode_1_add_r_imm), .asr_r_r(decode_opcode_1_asr_r_r),
    .eor_r_r(decode_opcode_1_eor_r_r), .lsl_r_r(decode_opcode_1_lsl_r_r), .lsr_r_r(decode_opcode_1_lsr_r_r),
    .mvn_r_r(decode_opcode_1_mvn_r_r), .neg_r_r(decode_opcode_1_neg_r_r), .orr_r_r(decode_opcode_1_orr_r_r),
    .sbc_r_r(sel_carry[1]), .sub_r_imm(decode_opcode_1_sub_r_imm),
    .ldrb_r_r_imm(decode_opcode_1_ldrb_r_r_imm), .strb_r_r_imm(decode_opcode_1_strb_r_r_imm),
    .ldrb_r_r_r(decode_opcode_1_ldrb_r_r_r), .strb_r_r_r(decode_opcode_1_strb_r_r_r),
    .bic_r_r(decode_opcode_1_bic_r_r), .cpy_r_r(decode_opcode_1_cpy_r_r),
    .mov_r_imm(decode_opcode_1_mov_r_imm), .mul_r_r(sel_op_alu[3]), .ror_r_r(sel_op_shift[2]),
    .tst_r_r(decode_opcode_1_tst_r_r), .bl_msb(decode_opcode_1_bl_msb), .bl_lsb(decode_opcode_1_bl_lsb));  // open: bx, mov_pc
  or bit1 (sel_op_shift[1], decode_opcode_1_lsl_r_r_imm, decode_opcode_1_lsr_r_r_imm, decode_opcode_1_lsl_r_r, decode_opcode_1_lsr_r_r);
  or bit0 (sel_op_shift[0], decode_opcode_1_asr_r_r_imm, decode_opcode_1_lsr_r_r_imm, decode_opcode_1_asr_r_r, decode_opcode_1_lsr_r_r);
  or u_sel_shift (sel_shift, decode_opcode_1_asr_r_r, decode_opcode_1_lsl_r_r, decode_opcode_1_lsr_r_r, sel_op_shift[2]);
  or bit2 (sel_op_alu[2], decode_opcode_1_eor_r_r, decode_opcode_1_mvn_r_r, decode_opcode_1_orr_r_r, decode_opcode_1_bic_r_r);
  or bit1_2 (sel_op_alu[1], decode_opcode_1_and_r_r, decode_opcode_1_sub_r_r_r, decode_opcode_1_sub_r_r_imm, decode_opcode_1_cmp_r_imm, decode_opcode_1_cmp_r_r, decode_opcode_1_mvn_r_r, decode_opcode_1_neg_r_r, sel_carry[1], decode_opcode_1_sub_r_imm, decode_opcode_1_bic_r_r, decode_opcode_1_tst_r_r);
  or bit0_2 (sel_op_alu[0], decode_opcode_1_add_r_r_r, decode_opcode_1_add_r_r_imm, decode_opcode_1_and_r_r, decode_opcode_1_ldrh_r_r_imm, decode_opcode_1_ldrh_r_r_r, decode_opcode_1_strh_r_r_imm, decode_opcode_1_strh_r_r_r, decode_opcode_1_b_cond, decode_opcode_1_b_incond, decode_opcode_1_cmn_r_r, sel_carry[0], decode_opcode_1_add_r_imm, decode_opcode_1_eor_r_r, decode_opcode_1_ldrb_r_r_imm, decode_opcode_1_ldrb_r_r_r, decode_opcode_1_strb_r_r_imm, decode_opcode_1_strb_r_r_r, decode_opcode_1_bic_r_r, decode_opcode_1_cpy_r_r, decode_opcode_1_mov_r_imm, decode_opcode_1_tst_r_r, decode_opcode_1_bl_msb, decode_opcode_1_bl_lsb);
  or or_1 (sel_operand_1, decode_opcode_1_neg_r_r, decode_opcode_1_cpy_r_r, decode_opcode_1_mov_r_imm, decode_opcode_1_bl_msb);
  or bit1_3 (sel_operand_2[1], decode_opcode_1_ldrh_r_r_imm, decode_opcode_1_strh_r_r_imm, decode_opcode_1_b_cond, decode_opcode_1_b_incond, decode_opcode_1_cmp_r_imm, decode_opcode_1_add_r_imm, decode_opcode_1_sub_r_imm, decode_opcode_1_ldrb_r_r_imm, decode_opcode_1_strb_r_r_imm, decode_opcode_1_mov_r_imm, decode_opcode_1_bl_msb, decode_opcode_1_bl_lsb);
  or bit0_3 (sel_operand_2[0], decode_opcode_1_add_r_r_imm, decode_opcode_1_sub_r_r_imm, decode_opcode_1_cmp_r_imm, decode_opcode_1_add_r_imm, decode_opcode_1_sub_r_imm, decode_opcode_1_mov_r_imm);
  or bit2_2 (sel_mult_2[2], decode_opcode_1_ldrb_r_r_imm, decode_opcode_1_strb_r_r_imm, decode_opcode_1_bl_msb);
  or bit1_4 (sel_mult_2[1], decode_opcode_1_b_cond, decode_opcode_1_bl_lsb);
  or bit0_4 (sel_mult_2[0], decode_opcode_1_b_incond, decode_opcode_1_bl_msb, decode_opcode_1_bl_lsb);
  or c_unaffected (cond_en, decode_opcode_1_lsl_r_r_imm, decode_opcode_1_asr_r_r, decode_opcode_1_lsl_r_r, decode_opcode_1_lsr_r_r);

  assign instruction_out = instruction_in;
endmodule

module Memory_Control (
  input  [15:0] instruction_in,
  output [15:0] instruction_out,
  output \byte ,
  output sel_mem,
  output str_data,
  output ldr_data,
  output flag_z_en,
  output flag_n_en,
  output flag_c_en,
  output flag_v_en,
  output sel_cpsr
);

  wire decode_opcode_1_adc_r_r, decode_opcode_1_add_r_imm, decode_opcode_1_add_r_r_imm,
       decode_opcode_1_add_r_r_r, decode_opcode_1_and_r_r, decode_opcode_1_asr_r_r,
       decode_opcode_1_asr_r_r_imm, decode_opcode_1_bic_r_r, decode_opcode_1_cmn_r_r,
       decode_opcode_1_cmp_r_imm, decode_opcode_1_cmp_r_r, decode_opcode_1_eor_r_r,
       decode_opcode_1_ldrb_r_r_imm, decode_opcode_1_ldrb_r_r_r, decode_opcode_1_ldrh_r_r_imm,
       decode_opcode_1_ldrh_r_r_r, decode_opcode_1_lsl_r_r, decode_opcode_1_lsl_r_r_imm,
       decode_opcode_1_lsr_r_r, decode_opcode_1_lsr_r_r_imm, decode_opcode_1_mov_r_imm,
       decode_opcode_1_mul_r_r, decode_opcode_1_mvn_r_r, decode_opcode_1_neg_r_r, decode_opcode_1_orr_r_r,
       decode_opcode_1_ror_r_r, decode_opcode_1_sbc_r_r, decode_opcode_1_strb_r_r_imm,
       decode_opcode_1_strb_r_r_r, decode_opcode_1_strh_r_r_imm, decode_opcode_1_strh_r_r_r,
       decode_opcode_1_sub_r_imm, decode_opcode_1_sub_r_r_imm, decode_opcode_1_sub_r_r_r,
       decode_opcode_1_tst_r_r;

  // Text text_1: pin names not known
  // Text text_2: pin names not known
  // Text text_3: pin names not known
  // Text text_4: pin names not known
  // Text text_5: pin names not known
  Decode_Opcode decode_opcode_1 (
    .instruction(instruction_in), .add_r_r_r(decode_opcode_1_add_r_r_r),
    .add_r_r_imm(decode_opcode_1_add_r_r_imm), .and_r_r(decode_opcode_1_and_r_r),
    .asr_r_r_imm(decode_opcode_1_asr_r_r_imm), .lsl_r_r_imm(decode_opcode_1_lsl_r_r_imm),
    .lsr_r_r_imm(decode_opcode_1_lsr_r_r_imm), .sub_r_r_r(decode_opcode_1_sub_r_r_r),
    .sub_r_r_imm(decode_opcode_1_sub_r_r_imm), .ldrh_r_r_imm(decode_opcode_1_ldrh_r_r_imm),
    .ldrh_r_r_r(decode_opcode_1_ldrh_r_r_r), .strh_r_r_imm(decode_opcode_1_strh_r_r_imm),
    .strh_r_r_r(decode_opcode_1_strh_r_r_r), .adc_r_r(decode_opcode_1_adc_r_r),
    .cmn_r_r(decode_opcode_1_cmn_r_r), .cmp_r_imm(decode_opcode_1_cmp_r_imm),
    .cmp_r_r(decode_opcode_1_cmp_r_r), .add_r_imm(decode_opcode_1_add_r_imm),
    .asr_r_r(decode_opcode_1_asr_r_r), .eor_r_r(decode_opcode_1_eor_r_r), .lsl_r_r(decode_opcode_1_lsl_r_r),
    .lsr_r_r(decode_opcode_1_lsr_r_r), .mvn_r_r(decode_opcode_1_mvn_r_r), .neg_r_r(decode_opcode_1_neg_r_r),
    .orr_r_r(decode_opcode_1_orr_r_r), .sbc_r_r(decode_opcode_1_sbc_r_r),
    .sub_r_imm(decode_opcode_1_sub_r_imm), .ldrb_r_r_imm(decode_opcode_1_ldrb_r_r_imm),
    .strb_r_r_imm(decode_opcode_1_strb_r_r_imm), .ldrb_r_r_r(decode_opcode_1_ldrb_r_r_r),
    .strb_r_r_r(decode_opcode_1_strb_r_r_r), .bic_r_r(decode_opcode_1_bic_r_r),
    .mov_r_imm(decode_opcode_1_mov_r_imm), .mul_r_r(decode_opcode_1_mul_r_r),
    .ror_r_r(decode_opcode_1_ror_r_r), .tst_r_r(decode_opcode_1_tst_r_r), .mov_pc(sel_cpsr));  // open: b_cond, b_incond, cpy_r_r, bl_msb, bl_lsb, bx
  or u_byte (\byte , decode_opcode_1_ldrb_r_r_imm, decode_opcode_1_ldrb_r_r_r, decode_opcode_1_strb_r_r_imm, decode_opcode_1_strb_r_r_r);
  or u_sel_mem (sel_mem, decode_opcode_1_ldrh_r_r_imm, decode_opcode_1_ldrh_r_r_r, decode_opcode_1_ldrb_r_r_imm, decode_opcode_1_ldrb_r_r_r);
  or u_str_data (str_data, decode_opcode_1_strh_r_r_imm, decode_opcode_1_strh_r_r_r, decode_opcode_1_strb_r_r_imm, decode_opcode_1_strb_r_r_r);
  or u_ldr_data (ldr_data, decode_opcode_1_ldrh_r_r_imm, decode_opcode_1_ldrh_r_r_r, decode_opcode_1_ldrb_r_r_imm, decode_opcode_1_ldrb_r_r_r);
  or u_flag_z_en (flag_z_en, decode_opcode_1_add_r_r_r, decode_opcode_1_add_r_r_imm, decode_opcode_1_and_r_r, decode_opcode_1_asr_r_r_imm, decode_opcode_1_lsl_r_r_imm, decode_opcode_1_lsr_r_r_imm, decode_opcode_1_sub_r_r_r, decode_opcode_1_sub_r_r_imm, decode_opcode_1_cmn_r_r, decode_opcode_1_cmp_r_imm, decode_opcode_1_cmp_r_r, decode_opcode_1_adc_r_r, decode_opcode_1_add_r_imm, decode_opcode_1_asr_r_r, decode_opcode_1_eor_r_r, decode_opcode_1_lsl_r_r, decode_opcode_1_lsr_r_r, decode_opcode_1_mvn_r_r, decode_opcode_1_neg_r_r, decode_opcode_1_orr_r_r, decode_opcode_1_sbc_r_r, decode_opcode_1_sub_r_imm, decode_opcode_1_bic_r_r, decode_opcode_1_mov_r_imm, decode_opcode_1_mul_r_r, decode_opcode_1_ror_r_r, decode_opcode_1_tst_r_r, sel_cpsr);
  or u_flag_n_en (flag_n_en, decode_opcode_1_add_r_r_r, decode_opcode_1_add_r_r_imm, decode_opcode_1_and_r_r, decode_opcode_1_asr_r_r_imm, decode_opcode_1_lsl_r_r_imm, decode_opcode_1_lsr_r_r_imm, decode_opcode_1_sub_r_r_r, decode_opcode_1_sub_r_r_imm, decode_opcode_1_cmn_r_r, decode_opcode_1_cmp_r_imm, decode_opcode_1_cmp_r_r, decode_opcode_1_adc_r_r, decode_opcode_1_add_r_imm, decode_opcode_1_asr_r_r, decode_opcode_1_eor_r_r, decode_opcode_1_lsl_r_r, decode_opcode_1_lsr_r_r, decode_opcode_1_mvn_r_r, decode_opcode_1_neg_r_r, decode_opcode_1_orr_r_r, decode_opcode_1_sbc_r_r, decode_opcode_1_sub_r_imm, decode_opcode_1_bic_r_r, decode_opcode_1_mov_r_imm, decode_opcode_1_mul_r_r, decode_opcode_1_ror_r_r, decode_opcode_1_tst_r_r, sel_cpsr);
  or u_flag_c_en (flag_c_en, decode_opcode_1_add_r_r_r, decode_opcode_1_add_r_r_imm, decode_opcode_1_asr_r_r_imm, decode_opcode_1_lsl_r_r_imm, decode_opcode_1_lsr_r_r_imm, decode_opcode_1_sub_r_r_r, decode_opcode_1_sub_r_r_imm, decode_opcode_1_cmn_r_r, decode_opcode_1_cmp_r_imm, decode_opcode_1_cmp_r_r, decode_opcode_1_adc_r_r, decode_opcode_1_add_r_imm, decode_opcode_1_asr_r_r, decode_opcode_1_lsl_r_r, decode_opcode_1_lsr_r_r, decode_opcode_1_neg_r_r, decode_opcode_1_sbc_r_r, decode_opcode_1_sub_r_imm, decode_opcode_1_ror_r_r, sel_cpsr);
  or u_flag_v_en (flag_v_en, decode_opcode_1_add_r_r_r, decode_opcode_1_add_r_r_imm, decode_opcode_1_sub_r_r_r, decode_opcode_1_sub_r_r_imm, decode_opcode_1_cmn_r_r, decode_opcode_1_cmp_r_imm, decode_opcode_1_cmp_r_r, decode_opcode_1_adc_r_r, decode_opcode_1_add_r_imm, decode_opcode_1_neg_r_r, decode_opcode_1_sbc_r_r, decode_opcode_1_sub_r_imm, sel_cpsr);

  assign instruction_out = instruction_in;
endmodule

module Writeback_Control (
  input  [15:0] instruction_in,
  output reg_bank_wr,
  output cond_en,
  output sel_PC
);

  wire decode_opcode_1_adc_r_r, decode_opcode_1_add_r_imm, decode_opcode_1_add_r_r_imm,
       decode_opcode_1_add_r_r_r, decode_opcode_1_and_r_r, decode_opcode_1_asr_r_r,
       decode_opcode_1_asr_r_r_imm, decode_opcode_1_b_incond, decode_opcode_1_bic_r_r,
       decode_opcode_1_bl_lsb, decode_opcode_1_bl_msb, decode_opcode_1_bx, decode_opcode_1_cpy_r_r,
       decode_opcode_1_eor_r_r, decode_opcode_1_ldrb_r_r_imm, decode_opcode_1_ldrb_r_r_r,
       decode_opcode_1_ldrh_r_r_imm, decode_opcode_1_ldrh_r_r_r, decode_opcode_1_lsl_r_r,
       decode_opcode_1_lsl_r_r_imm, decode_opcode_1_lsr_r_r, decode_opcode_1_lsr_r_r_imm,
       decode_opcode_1_mov_pc, decode_opcode_1_mov_r_imm, decode_opcode_1_mul_r_r, decode_opcode_1_mvn_r_r,
       decode_opcode_1_neg_r_r, decode_opcode_1_orr_r_r, decode_opcode_1_ror_r_r, decode_opcode_1_sbc_r_r,
       decode_opcode_1_sub_r_imm, decode_opcode_1_sub_r_r_imm, decode_opcode_1_sub_r_r_r;

  // Text text_1: pin names not known
  // Text text_2: pin names not known
  // Text text_3: pin names not known
  // Text text_4: pin names not known
  // Text text_5: pin names not known
  Decode_Opcode decode_opcode_1 (
    .instruction(instruction_in), .add_r_r_r(decode_opcode_1_add_r_r_r),
    .add_r_r_imm(decode_opcode_1_add_r_r_imm), .and_r_r(decode_opcode_1_and_r_r),
    .asr_r_r_imm(decode_opcode_1_asr_r_r_imm), .lsl_r_r_imm(decode_opcode_1_lsl_r_r_imm),
    .lsr_r_r_imm(decode_opcode_1_lsr_r_r_imm), .sub_r_r_r(decode_opcode_1_sub_r_r_r),
    .sub_r_r_imm(decode_opcode_1_sub_r_r_imm), .ldrh_r_r_imm(decode_opcode_1_ldrh_r_r_imm),
    .ldrh_r_r_r(decode_opcode_1_ldrh_r_r_r), .b_cond(cond_en), .b_incond(decode_opcode_1_b_incond),
    .adc_r_r(decode_opcode_1_adc_r_r), .add_r_imm(decode_opcode_1_add_r_imm),
    .asr_r_r(decode_opcode_1_asr_r_r), .eor_r_r(decode_opcode_1_eor_r_r), .lsl_r_r(decode_opcode_1_lsl_r_r),
    .lsr_r_r(decode_opcode_1_lsr_r_r), .mvn_r_r(decode_opcode_1_mvn_r_r), .neg_r_r(decode_opcode_1_neg_r_r),
    .orr_r_r(decode_opcode_1_orr_r_r), .sbc_r_r(decode_opcode_1_sbc_r_r),
    .sub_r_imm(decode_opcode_1_sub_r_imm), .ldrb_r_r_imm(decode_opcode_1_ldrb_r_r_imm),
    .ldrb_r_r_r(decode_opcode_1_ldrb_r_r_r), .bic_r_r(decode_opcode_1_bic_r_r),
    .cpy_r_r(decode_opcode_1_cpy_r_r), .mov_r_imm(decode_opcode_1_mov_r_imm),
    .mul_r_r(decode_opcode_1_mul_r_r), .ror_r_r(decode_opcode_1_ror_r_r), .bl_msb(decode_opcode_1_bl_msb),
    .bl_lsb(decode_opcode_1_bl_lsb), .bx(decode_opcode_1_bx), .mov_pc(decode_opcode_1_mov_pc));  // open: strh_r_r_imm, strh_r_r_r, cmn_r_r, cmp_r_imm, cmp_r_r, strb_r_r_imm, strb_r_r_r, tst_r_r
  or u_reg_bank_wr (reg_bank_wr, decode_opcode_1_add_r_r_r, decode_opcode_1_add_r_r_imm, decode_opcode_1_and_r_r, decode_opcode_1_asr_r_r_imm, decode_opcode_1_lsl_r_r_imm, decode_opcode_1_lsr_r_r_imm, decode_opcode_1_sub_r_r_r, decode_opcode_1_sub_r_r_imm, decode_opcode_1_ldrh_r_r_imm, decode_opcode_1_ldrh_r_r_r, decode_opcode_1_adc_r_r, decode_opcode_1_add_r_imm, decode_opcode_1_asr_r_r, decode_opcode_1_eor_r_r, decode_opcode_1_lsl_r_r, decode_opcode_1_lsr_r_r, decode_opcode_1_mvn_r_r, decode_opcode_1_neg_r_r, decode_opcode_1_orr_r_r, decode_opcode_1_sbc_r_r, decode_opcode_1_sub_r_imm, decode_opcode_1_ldrb_r_r_imm, decode_opcode_1_ldrb_r_r_r, decode_opcode_1_bic_r_r, decode_opcode_1_cpy_r_r, decode_opcode_1_mov_r_imm, decode_opcode_1_mul_r_r, decode_opcode_1_ror_r_r);
  or u_sel_PC (sel_PC, cond_en, decode_opcode_1_b_incond, decode_opcode_1_bl_msb, decode_opcode_1_bl_lsb, decode_opcode_1_bx, decode_opcode_1_mov_pc);
endmodule

module Branch_Control (
  input  [15:0] instruction_in,
  output out_2,
  output out_3,
  output sel_pc
);

  wire decode_opcode_1_adc_r_r, decode_opcode_1_add_r_imm, decode_opcode_1_add_r_r_imm,
       decode_opcode_1_add_r_r_r, decode_opcode_1_and_r_r, decode_opcode_1_asr_r_r,
       decode_opcode_1_asr_r_r_imm, decode_opcode_1_b_incond, decode_opcode_1_bic_r_r,
       decode_opcode_1_bl_lsb, decode_opcode_1_bl_msb, decode_opcode_1_bx, decode_opcode_1_cpy_r_r,
       decode_opcode_1_eor_r_r, decode_opcode_1_ldrb_r_r_imm, decode_opcode_1_ldrb_r_r_r,
       decode_opcode_1_ldrh_r_r_imm, decode_opcode_1_ldrh_r_r_r, decode_opcode_1_lsl_r_r,
       decode_opcode_1_lsl_r_r_imm, decode_opcode_1_lsr_r_r, decode_opcode_1_lsr_r_r_imm,
       decode_opcode_1_mov_pc, decode_opcode_1_mov_r_imm, decode_opcode_1_mul_r_r, decode_opcode_1_mvn_r_r,
       decode_opcode_1_neg_r_r, decode_opcode_1_orr_r_r, decode_opcode_1_ror_r_r, decode_opcode_1_sbc_r_r,
       decode_opcode_1_sub_r_imm, decode_opcode_1_sub_r_r_imm, decode_opcode_1_sub_r_r_r;

  // Text text_1: pin names not known
  // Text text_2: pin names not known
  // Text text_3: pin names not known
  // Text text_4: pin names not known
  // Text text_5: pin names not known
  Decode_Opcode decode_opcode_1 (
    .instruction(instruction_in), .add_r_r_r(decode_opcode_1_add_r_r_r),
    .add_r_r_imm(decode_opcode_1_add_r_r_imm), .and_r_r(decode_opcode_1_and_r_r),
    .asr_r_r_imm(decode_opcode_1_asr_r_r_imm), .lsl_r_r_imm(decode_opcode_1_lsl_r_r_imm),
    .lsr_r_r_imm(decode_opcode_1_lsr_r_r_imm), .sub_r_r_r(decode_opcode_1_sub_r_r_r),
    .sub_r_r_imm(decode_opcode_1_sub_r_r_imm), .ldrh_r_r_imm(decode_opcode_1_ldrh_r_r_imm),
    .ldrh_r_r_r(decode_opcode_1_ldrh_r_r_r), .b_cond(out_3), .b_incond(decode_opcode_1_b_incond),
    .adc_r_r(decode_opcode_1_adc_r_r), .add_r_imm(decode_opcode_1_add_r_imm),
    .asr_r_r(decode_opcode_1_asr_r_r), .eor_r_r(decode_opcode_1_eor_r_r), .lsl_r_r(decode_opcode_1_lsl_r_r),
    .lsr_r_r(decode_opcode_1_lsr_r_r), .mvn_r_r(decode_opcode_1_mvn_r_r), .neg_r_r(decode_opcode_1_neg_r_r),
    .orr_r_r(decode_opcode_1_orr_r_r), .sbc_r_r(decode_opcode_1_sbc_r_r),
    .sub_r_imm(decode_opcode_1_sub_r_imm), .ldrb_r_r_imm(decode_opcode_1_ldrb_r_r_imm),
    .ldrb_r_r_r(decode_opcode_1_ldrb_r_r_r), .bic_r_r(decode_opcode_1_bic_r_r),
    .cpy_r_r(decode_opcode_1_cpy_r_r), .mov_r_imm(decode_opcode_1_mov_r_imm),
    .mul_r_r(decode_opcode_1_mul_r_r), .ror_r_r(decode_opcode_1_ror_r_r), .bl_msb(decode_opcode_1_bl_msb),
    .bl_lsb(decode_opcode_1_bl_lsb), .bx(decode_opcode_1_bx), .mov_pc(decode_opcode_1_mov_pc));  // open: strh_r_r_imm, strh_r_r_r, cmn_r_r, cmp_r_imm, cmp_r_r, strb_r_r_imm, strb_r_r_r, tst_r_r
  or or_1 (out_2, decode_opcode_1_add_r_r_r, decode_opcode_1_add_r_r_imm, decode_opcode_1_and_r_r, decode_opcode_1_asr_r_r_imm, decode_opcode_1_lsl_r_r_imm, decode_opcode_1_lsr_r_r_imm, decode_opcode_1_sub_r_r_r, decode_opcode_1_sub_r_r_imm, decode_opcode_1_ldrh_r_r_imm, decode_opcode_1_ldrh_r_r_r, decode_opcode_1_adc_r_r, decode_opcode_1_add_r_imm, decode_opcode_1_asr_r_r, decode_opcode_1_eor_r_r, decode_opcode_1_lsl_r_r, decode_opcode_1_lsr_r_r, decode_opcode_1_mvn_r_r, decode_opcode_1_neg_r_r, decode_opcode_1_orr_r_r, decode_opcode_1_sbc_r_r, decode_opcode_1_sub_r_imm, decode_opcode_1_ldrb_r_r_imm, decode_opcode_1_ldrb_r_r_r, decode_opcode_1_bic_r_r, decode_opcode_1_cpy_r_r, decode_opcode_1_mov_r_imm, decode_opcode_1_mul_r_r, decode_opcode_1_ror_r_r);
  or or_2 (sel_pc, out_3, decode_opcode_1_b_incond, decode_opcode_1_bl_msb, decode_opcode_1_bl_lsb, decode_opcode_1_bx, decode_opcode_1_mov_pc);
endmodule

module Multi_2 (
  input  [4:0] immediate5,
  input  [2:0] sel_mul_2,
  input  [10:0] offset_incond,
  input  [7:0] offset_cond,
  output [15:0] Mult_2_out
);

  wire [15:0] adder_1_out, adder_2_out, adder_3_out, bit_extender_1_out, bit_extender_2_out,
       bit_extender_3_out, bit_extender_4_out, multiplexer_1_out, shifter_1_out, shifter_2_out;

  // Text text_1: pin names not known
  // Text text_2: pin names not known
  // Text text_3: pin names not known
  // Text text_4: pin names not known
  // Text text_5: pin names not known
  assign bit_extender_1_out = {{11{1'b0}}, immediate5};  // Bit_Extender bit_extender_1
  assign bit_extender_2_out = {{5{offset_incond[10]}}, offset_incond};  // Bit_Extender bit_extender_2
  assign bit_extender_3_out = {{5{1'b0}}, offset_incond};  // Bit_Extender bit_extender_3
  assign bit_extender_4_out = {{8{offset_cond[7]}}, offset_cond};  // Bit_Extender bit_extender_4
  Adder #(.width(16)) adder_1 (.a(bit_extender_2_out), .b(16'h1), .out(adder_1_out));  // open: cin, cout
  Adder #(.width(16)) adder_2 (.a(bit_extender_3_out), .b(16'h2), .out(adder_2_out));  // open: cin, cout
  Adder #(.width(16)) adder_3 (.a(bit_extender_4_out), .b(16'h1), .out(adder_3_out));  // open: cin, cout
  Multiplexer #(.select(2), .width(16), .enable("false")) multiplexer_1 (
    .in0(bit_extender_1_out), .in1(adder_1_out), .in2(adder_3_out), .in3(adder_2_out),
    .out(multiplexer_1_out), .sel(sel_mul_2[1:0]));
  Shifter #(.width(16)) shifter_1 (.in(multiplexer_1_out), .\dist (4'b0001), .out(shifter_1_out));
  Shifter #(.width(16)) shifter_2 (.in(bit_extender_2_out), .\dist (4'b1100), .out(shifter_2_out));
  Multiplexer #(.select(3), .width(16), .enable("false")) multiplexer_2 (
    .in0(shifter_1_out), .in1(shifter_1_out), .in2(shifter_1_out), .in3(shifter_1_out),
    .in4(bit_extender_1_out), .in5(shifter_2_out), .out(Mult_2_out), .sel(sel_mul_2));  // open: in6, in7

  // Notes on the sheet:
  //   rajouté le bit de signe.
  //   Multi_2 v1.2
  //   alors que les offset servent aux instructions de branch.
  //   Ajout 1.1 : Ajout d'un shift de 11 gauche pour l'offset du BL MSB
  //   L'offset inconditionnelle a besoin des 2 extensions posibbles :
  //   Ajout 1.2 : Changement de la correction du PC pour + 2 à la place de + 4
  //   Le branch classique peut faire des saut en arrière, et on a donc besoin d'une extension signée.
  //   Ce bloc sert à multiplier une des valeurs en entrée par 2. L'immediate5 sert pour les STR et LDR, 
  //   Le Branch avec Link peut utilisé cet offset en tant que LSB, et on l'additionnera ensuite au PC. Il ne faut donc pas 
  //   Correction du PC qui n'est pas pré-incrémenter
  //   pour LDRB et STRB.
  //   L'opération 100 est utilsée par BL MSB : On récupère les 5 bits MSB de l'offset décalé de 12 à gauche.
  //   Permet de ne pas multiplier par 2 la valeur immediate sur 5 bits
endmodule

module Execution (
  input  [15:0] reg_data_n_in,
  input  [4:0] immediate5,
  input  alu_en,
  input  clock,
  input  reset,
  input  [10:0] offset_incond,
  input  [7:0] offset_cond_or_immediate8,
  input  interrupt_en,
  input  [15:0] reg_data_m_in,
  input  [2:0] immediate3,
  input  spsr_irq_en,
  input  [21:0] execute_control_bus,
  output [15:0] jump_adr,
  output [15:0] data_out,
  output [4:0] out_15
);

  wire alu_1_borrow_sub_out, alu_1_carry_add_out, c_unaffected, carry, carry_shift, multiplexer_4_out,
       not_1_out;
  wire [3:0] comparator_1_eq, multiplexer_5_out, spsr_1_spsr_irq;
  wire [4:0] multiplexer_2_out;
  wire [15:0] bit_extender_1_out, bit_extender_2_out, multi_2_1_mult_2_out, multiplexer_1_out, op_1, op_2;

  // Text text_1: pin names not known
  // Text text_2: pin names not known
  // Text text_3: pin names not known
  // Text text_4: pin names not known
  // Text text_5: pin names not known
  assign bit_extender_1_out = {{8{1'b0}}, offset_cond_or_immediate8};  // Bit_Extender bit_extender_1
  assign bit_extender_2_out = {{13{1'b0}}, immediate3};  // Bit_Extender bit_extender_2
  Multiplexer #(.width(16), .enable("false")) multiplexer_1 (
    .in0(reg_data_n_in), .in1({16{1'b0}}), .out(multiplexer_1_out), .sel(execute_control_bus[9]));
  Multi_2 multi_2_1 (
    .immediate5(immediate5), .sel_mul_2(execute_control_bus[12:10]), .offset_incond(offset_incond),
    .offset_cond(offset_cond_or_immediate8), .Mult_2_out(multi_2_1_mult_2_out));
  Multiplexer #(.width(5), .enable("false")) multiplexer_2 (
    .in0(immediate5), .in1(reg_data_m_in[4:0]), .out(multiplexer_2_out), .sel(execute_control_bus[19]));
  Shift shift_1 (
    .sel_op_shift(execute_control_bus[2:0]), .operand_1(multiplexer_1_out), .operand_2(multiplexer_2_out),
    .data_shift_out(op_1), .carry_shift(carry_shift), .shift_c_unaffected(execute_control_bus[20]),
    .c_unaffected(c_unaffected));
  Multiplexer #(.select(2), .width(16), .enable("false")) multiplexer_3 (
    .in0(reg_data_m_in), .in1(bit_extender_2_out), .in2(multi_2_1_mult_2_out), .in3(bit_extender_1_out),
    .out(op_2), .sel(execute_control_bus[8:7]));
  not not_1 (not_1_out, carry);
  Multiplexer #(.select(2), .enable("false")) multiplexer_4 (
    .in0(1'b0), .in1(carry), .in2(not_1_out), .out(multiplexer_4_out), .sel(execute_control_bus[18:17]));  // open: in3
  ALU alu_1 (
    .sel_op_alu(execute_control_bus[6:3]), .operand_1(op_1), .operand_2(op_2), .data_out(jump_adr),
    .carry_add_out(alu_1_carry_add_out), .carry_in(multiplexer_4_out), .borrow_sub_out(alu_1_borrow_sub_out));
  Register #(.width(16)) Execute_Data_Out (.D(jump_adr), .en(alu_en), .clk(clock), .Q(data_out), .clr(reset));
  Comparator #(.width(16), .mode("unsigned")) comparator_1 (
    .a(data_out), .b({16{1'b0}}), .eq(comparator_1_eq[0]));  // open: gt, lt
  Gestion_Carry gestion_carry_1 (
    .carry_add(alu_1_carry_add_out), .borrow_sub(alu_1_borrow_sub_out), .carry(comparator_1_eq[2]),
    .overflow(comparator_1_eq[3]), .operand_1(op_1), .operand_2(op_2), .op_alu(execute_control_bus[6:3]),
    .carry_shift(carry_shift), .op_shift(execute_control_bus[2:0]), .c_flag(carry), .RST(reset),
    .c_unaffected(c_unaffected), .alu_en(alu_en), .clock(clock));
  Multiplexer #(.width(4), .enable("false")) multiplexer_5 (
    .in0({comparator_1_eq[3:2], data_out[15], comparator_1_eq[0]}), .in1(spsr_1_spsr_irq),
    .out(multiplexer_5_out), .sel(execute_control_bus[21]));
  CPSR1 CPSR_P (
    .flag_en(execute_control_bus[16:13]), .cpsr_out(out_15), .carry(carry), .reset(reset),
    .cpsr_in(multiplexer_5_out), .clock(clock), .interrupt_en(interrupt_en),
    .retour_jump(execute_control_bus[21]));
  SPSR spsr_1 (.spsr_irq_en(spsr_irq_en), .cpsr(out_15), .spsr_irq(spsr_1_spsr_irq), .clock(clock), .reset(reset));

  // Other names for the same wires on the sheet: CLK = clock; sel_op_shift[2:0] = execute_control_bus[2:0];
  //   sel_op_alu[3:0] = execute_control_bus[6:3]; sel_operand_2[1:0] = execute_control_bus[8:7];
  //   sel_operand_1 = execute_control_bus[9]; sel_mult_2[2:0] = execute_control_bus[12:10];
  //   flag_en[3:0] = execute_control_bus[16:13]; sel_carry[1:0] = execute_control_bus[18:17];
  //   sel_shift = execute_control_bus[19]; shift_c_unaffected = execute_control_bus[20];
  //   sel_cpsr = execute_control_bus[21]; RST = reset

  // Notes on the sheet:
  //   EXECUTION v1.1
  //   Ce bloc s'occupe de traiter mathématiquement les données.
  //   Les divers signaux de contrôles permettent de sélectionner les bonnes valeurs et opérations.
  //   Table des opérations du SHIFT :
  //   000 : Bypass du SHIFT avec operand_1
  //   010 : operand_1 logical left avec operand 2
  //   001 : operand_1 arithmetic right avec operand_2
  //   011 : operand_1 logical right avec operand_2
  //   100 : operand_1 rotation right avec operand_2
  //   Table des opérations de l'ALU :
  //   0000 : Bypass de l'ALU avec operand_1
  //   0001 : data_out = operand_1 + operand_2
  //   0010 : data_out = operand_1 - operand_2
  //   0011 : data_out = operand_1 AND operand_2
  //   0100 : data_out = operand_1 OR operand_2
  //   0101 : data_out = operand_1 XOR operand_2
  //   0110 : data_out = NOT operand_1
  //   1000 : data_out = operand_1 * operand_2
  //   0111 : data_out = operand_1 AND (NOT operand_2)
  //   et on met tout les enable actif pour le CPSR.
  //   Si un SUB PC, lR est en cours, on sélectionne le SPSR comme entrée au CPSR
  //   L'écriture du CPSR s'effectue pendant l'accès mémoire
endmodule

module ALU (
  input  [3:0] sel_op_alu,
  input  [15:0] operand_1,
  input  carry_in,
  input  [15:0] operand_2,
  output carry_add_out,
  output [15:0] data_out,
  output borrow_sub_out
);

  wire [15:0] adder_1_out, and_1_out, and_2_out, multiplier_1_out, not_1_out, not_2_out, or_1_out,
       subtractor_1_out, xor_1_out;

  // Text text_1: pin names not known
  // Text text_2: pin names not known
  // Text text_3: pin names not known
  // Text text_4: pin names not known
  // Text text_5: pin names not known
  Adder #(.width(16)) adder_1 (.a(operand_1), .b(operand_2), .out(adder_1_out), .cin(carry_in), .cout(carry_add_out));
  Subtractor #(.width(16)) subtractor_1 (
    .a(operand_1), .b(operand_2), .out(subtractor_1_out), .bin(carry_in), .bout(borrow_sub_out));
  assign and_1_out = operand_1 & operand_2;  // AND_Gate and_1, 16 bits wide
  assign or_1_out = operand_1 | operand_2;  // OR_Gate or_1, 16 bits wide
  assign not_1_out = ~operand_1;  // NOT_Gate not_1, 16 bits wide
  assign and_2_out = operand_1 & not_2_out;  // AND_Gate and_2, 16 bits wide
  assign not_2_out = ~operand_2;  // NOT_Gate not_2, 16 bits wide
  Multiplier #(.width(16)) multiplier_1 (.a(operand_1), .b(operand_2), .out(multiplier_1_out));  // open: cin, cout
  assign xor_1_out = operand_1 ^ operand_2;  // XOR_Gate xor_1, 16 bits wide
  Multiplexer #(.select(4), .width(16), .enable("false")) multiplexer_1 (
    .in0(operand_1), .in1(adder_1_out), .in2(subtractor_1_out), .in3(and_1_out), .in4(or_1_out),
    .in5(xor_1_out), .in6(not_1_out), .in7(and_2_out), .in8(multiplier_1_out), .in9({16{1'b0}}),
    .in10({16{1'b0}}), .in11({16{1'b0}}), .in12({16{1'b0}}), .in13({16{1'b0}}), .in14({16{1'b0}}),
    .in15({16{1'b0}}), .out(data_out), .sel(sel_op_alu));

  // Notes on the sheet:
  //   ALU v1.0
  //   Contient les blocs d'opérations (addition, soustraction, ...) ainsi
  //   que les opérations logique (ET, OU, ...).
endmodule

module Shift (
  input  [2:0] sel_op_shift,
  input  [15:0] operand_1,
  input  [4:0] operand_2,
  input  shift_c_unaffected,
  output [15:0] data_shift_out,
  output carry_shift,
  output c_unaffected
);

  wire comparator_1_eq;
  wire [2:0] subtractor_3_out;
  wire [3:0] multiplexer_2_out;
  wire [4:0] subtractor_1_out, subtractor_2_out;
  wire [15:0] shifter_1_out, shifter_2_out, shifter_3_out, shifter_4_out;

  // Text text_1: pin names not known
  // Text text_2: pin names not known
  // Text text_3: pin names not known
  // Text text_4: pin names not known
  // Text text_5: pin names not known
  Subtractor #(.width(5)) subtractor_1 (.a(operand_2), .b(5'b00001), .out(subtractor_1_out));  // open: bin, bout
  Subtractor #(.width(5)) subtractor_2 (.a(5'b10000), .b(operand_2), .out(subtractor_2_out));  // open: bin, bout
  Comparator #(.width(5)) comparator_1 (.a(operand_2), .b({5{1'b0}}), .eq(comparator_1_eq));  // open: gt, lt
  Shifter #(.width(16), .shift("ar")) shifter_1 (.in(operand_1), .\dist (operand_2[3:0]), .out(shifter_1_out));
  Shifter #(.width(16)) shifter_2 (.in(operand_1), .\dist (operand_2[3:0]), .out(shifter_2_out));
  Shifter #(.width(16), .shift("lr")) shifter_3 (.in(operand_1), .\dist (operand_2[3:0]), .out(shifter_3_out));
  Shifter #(.width(16), .shift("rr")) shifter_4 (.in(operand_1), .\dist (operand_2[3:0]), .out(shifter_4_out));
  and and_1 (c_unaffected, comparator_1_eq, shift_c_unaffected);
  Multiplexer #(.select(3), .width(16), .enable("false")) multiplexer_1 (
    .in0(operand_1), .in1(shifter_1_out), .in2(shifter_2_out), .in3(shifter_3_out), .in4(shifter_4_out),
    .in5({16{1'b0}}), .in6({16{1'b0}}), .in7({16{1'b0}}), .out(data_shift_out), .sel(sel_op_shift));
  Subtractor #(.width(3)) subtractor_3 (.a(sel_op_shift), .b(3'b001), .out(subtractor_3_out));  // open: bin, bout
  Multiplexer #(.select(2), .width(4), .enable("false")) multiplexer_2 (
    .in0(subtractor_1_out[3:0]), .in1(subtractor_2_out[3:0]), .in2(subtractor_1_out[3:0]),
    .in3(subtractor_1_out[3:0]), .out(multiplexer_2_out), .sel(subtractor_3_out[1:0]));
  Multiplexer #(.select(4), .enable("false")) multiplexer_3 (
    .in0(operand_1[0]), .in1(operand_1[1]), .in2(operand_1[2]), .in3(operand_1[3]), .in4(operand_1[4]),
    .in5(operand_1[5]), .in6(operand_1[6]), .in7(operand_1[7]), .in8(operand_1[8]), .in9(operand_1[9]),
    .in10(operand_1[10]), .in11(operand_1[11]), .in12(operand_1[12]), .in13(operand_1[13]),
    .in14(operand_1[14]), .in15(operand_1[15]), .out(carry_shift), .sel(multiplexer_2_out));

  // Notes on the sheet:
  //   SHIFT v1.0
  //   Gère le décalage de bits logique gauch et droite, ainsi que arithmetique.
  //   Si l'operand vaut 0 (Qui est la condition pour ne pas mettre à jour le flag C),
  //   Gestion du flag C des shifts
  //   shift_c_unaffected permet de préciser si l'instruction de shift peut ne pas mettre à jour le flag de carry.
  //   et que l'instruction peut ne pas mettre à jour, alors on active c_unaffected qui contrôlera la mise à jour.
  //   Le décalage est sur 5 bits, même si cela n'est pas utile pour le Thumb Code.
  //   En effet, avec des données sur 16 bits, une valeur de 4 bits auraient suffit. 
  //   Seullement, le Thumb Code est prévu pour être utilisé avec du ARM Code classique, et donc sur 32 bits.
  //   On s'occupe de sélectionner le carry de l'opération en cours. Diffère si shift gauche ou droite principalement.
endmodule

module Gestion_Carry (
  input  [3:0] op_alu,
  input  c_unaffected,
  input  [2:0] op_shift,
  input  c_flag,
  input  carry_add,
  input  borrow_sub,
  input  carry_shift,
  input  alu_en,
  input  [15:0] operand_1,
  input  [15:0] operand_2,
  input  clock,
  input  RST,
  output carry,
  output overflow
);

  wire adder_1_cout, comparator_1_gt, multiplexer_2_out, multiplexer_3_out, not_1_out, subtractor_1_bout,
       xor_1_out, xor_2_out, xor_3_out;
  wire [1:0] multiplexer_1_out;

  // Text text_1: pin names not known
  // Text text_2: pin names not known
  // Text text_3: pin names not known
  // Text text_4: pin names not known
  // Text text_5: pin names not known
  Comparator #(.width(3), .mode("unsigned")) comparator_1 (
    .a(op_shift), .b(3'b000), .gt(comparator_1_gt));  // open: eq, lt
  Adder #(.width(15)) adder_1 (.a(operand_1[14:0]), .b(operand_2[14:0]), .cout(adder_1_cout));  // open: out, cin
  Subtractor #(.width(15)) subtractor_1 (
    .a(operand_1[14:0]), .b(operand_2[14:0]), .bout(subtractor_1_bout));  // open: out, bin
  xor xor_1 (xor_1_out, c_unaffected, comparator_1_gt);
  Multiplexer #(.width(2), .enable("false")) multiplexer_1 (
    .in0(op_alu[1:0]), .in1(2'b11), .out(multiplexer_1_out), .sel(xor_1_out));
  Multiplexer #(.select(2), .enable("false")) multiplexer_2 (
    .in0(c_flag), .in1(carry_add), .in2(not_1_out), .in3(carry_shift), .out(multiplexer_2_out),
    .sel(multiplexer_1_out));
  not not_1 (not_1_out, borrow_sub);
  xor xor_2 (xor_2_out, carry_add, adder_1_cout);
  xor xor_3 (xor_3_out, borrow_sub, subtractor_1_bout);
  Multiplexer #(.select(2), .enable("false")) multiplexer_3 (
    .in0(1'b0), .in1(xor_2_out), .in2(xor_3_out), .in3(1'b0), .out(multiplexer_3_out), .sel(multiplexer_1_out));
  Register #(.width(1)) register_1 (.D(multiplexer_2_out), .en(alu_en), .clk(clock), .Q(carry), .clr(RST));
  Register #(.width(1)) register_2 (.D(multiplexer_3_out), .en(alu_en), .clk(clock), .Q(overflow), .clr(RST));

  // Notes on the sheet:
  //   GESTION CARRY/OVERFLOW v1.0
  //   Si il y a opération de shift, alors on va sélectionner le carry_shift.
  //   (Excepetion faîtes si c_unaffected est généré par le shift.)
  //   une addition ou une soustraction qui est en cours. 
  //   Si rien de tout ça, le flag C est resélectionné et bouclé sur lui même
  //   Sinon, on prend les 2 premiers bits de l'opération de l'ALU, qui nous indiquera si c'est
  //   Le flag C est rebouclé sur lui-même, car dans certains shift, il reste inchangé
  //   GESTION DE L'OVERFLOW
  //   Cn XOR Cn - 1 = Overflow
endmodule

module CPSR1 (
  input  [3:0] cpsr_in,
  input  [3:0] flag_en,
  input  clock,
  input  interrupt_en,
  input  retour_jump,
  input  reset,
  output [4:0] cpsr_out,
  output carry
);

  // Text text_1: pin names not known
  // Text text_2: pin names not known
  // Text text_3: pin names not known
  // Text text_4: pin names not known
  // Text text_5: pin names not known
  Register #(.width(1)) N (.D(cpsr_in[1]), .en(flag_en[1]), .clk(clock), .Q(cpsr_out[1]), .clr(reset));
  Register #(.width(1)) C (.D(cpsr_in[2]), .en(flag_en[2]), .clk(clock), .Q(carry), .clr(reset));
  Register #(.width(1)) V (.D(cpsr_in[3]), .en(flag_en[3]), .clk(clock), .Q(cpsr_out[3]), .clr(reset));
  Register #(.width(1)) Z (.D(cpsr_in[0]), .en(flag_en[0]), .clk(clock), .Q(cpsr_out[0]), .clr(reset));
  S_R_Flip_Flop s_r_ff_1 (
    .S(interrupt_en), .R(retour_jump), .clk(clock), .Q(cpsr_out[4]), .reset(reset));  // open: Qn, preset

  assign cpsr_out[2] = carry;

  // Notes on the sheet:
  //   CPSR v1.1
  //   Current Program State Register
  //   Enregistre les informations relatives à l'état courant du programme.
endmodule

module SPSR (
  input  spsr_irq_en,
  input  [4:0] cpsr,
  input  clock,
  input  reset,
  output [3:0] spsr_irq
);

  // Text text_1: pin names not known
  // Text text_2: pin names not known
  // Text text_3: pin names not known
  // Text text_4: pin names not known
  // Text text_5: pin names not known
  Register #(.width(1)) Z (.D(cpsr[0]), .en(spsr_irq_en), .clk(clock), .Q(spsr_irq[0]), .clr(reset));
  Register #(.width(1)) N (.D(cpsr[1]), .en(spsr_irq_en), .clk(clock), .Q(spsr_irq[1]), .clr(reset));
  Register #(.width(1)) C (.D(cpsr[2]), .en(spsr_irq_en), .clk(clock), .Q(spsr_irq[2]), .clr(reset));
  Register #(.width(1)) V (.D(cpsr[3]), .en(spsr_irq_en), .clk(clock), .Q(spsr_irq[3]), .clr(reset));

  // Notes on the sheet:
  //   SPSR_irq v1.1
  //   Saved Program State Register
  //   Ainsi, la routine peut utiliser le CPSR, et restorera le SPSR une fois qu'elle sera terminée.
  //   Enregistre les informations relatives à l'état courant du programme, juste avant l'appel de l'interruption.
endmodule

module Memory_Access (
  input  [15:0] mem_data_in,
  input  [15:0] reg_data_in,
  input  clock,
  input  mem_en,
  input  reset,
  input  [15:0] data_in,
  input  [3:0] mem_control_bus,
  output [14:0] mem_data_adr,
  output [15:0] mem_data_out,
  output High_Byte,
  output Low_Byte,
  output str_data,
  output ldr_data,
  output [15:0] mem_out
);

  wire adresse_offset, and_1_out, and_2_out, not_1_out, not_2_out, or_1_out;
  wire [15:0] multiplexer_2_out, register_1_q;

  // Text text_1: pin names not known
  // Text text_2: pin names not known
  // Text text_3: pin names not known
  // Text text_4: pin names not known
  // Text text_5: pin names not known
  Register #(.width(16)) register_1 (
    .D({mem_data_adr, adresse_offset}), .en(1'b1), .clk(clock), .Q(register_1_q), .clr(reset));
  Multiplexer #(.width(16), .enable("false")) multiplexer_1 (
    .in0(register_1_q), .in1(data_in), .out({mem_data_adr, adresse_offset}), .sel(or_1_out));
  or or_1 (or_1_out, mem_control_bus[1], mem_control_bus[2]);
  Multiplexer #(.width(16), .enable("false")) multiplexer_2 (
    .in0(data_in), .in1(mem_data_in), .out(multiplexer_2_out), .sel(mem_control_bus[0]));
  not not_1 (not_1_out, adresse_offset);
  not not_2 (not_2_out, mem_control_bus[3]);
  and and_1 (and_1_out, mem_control_bus[3], adresse_offset);
  and and_2 (and_2_out, mem_control_bus[3], not_1_out);
  and and_3 (ldr_data, mem_control_bus[2], mem_en);
  Register #(.width(16)) Memory_Data_Out (.D(multiplexer_2_out), .en(mem_en), .clk(clock), .Q(mem_out), .clr(reset));
  or or_2 (High_Byte, not_2_out, and_1_out);
  or or_3 (Low_Byte, not_2_out, and_2_out);
  and and_4 (str_data, mem_control_bus[1], mem_en);

  assign mem_data_out = reg_data_in;

  // Other names for the same wires on the sheet: CLK = clock; sel_mem = mem_control_bus[0];
  //   str_data_t = mem_control_bus[1]; ldr_data_t = mem_control_bus[2]; byte = mem_control_bus[3]; RST = reset

  // Notes on the sheet:
  //   MEMORY ACCESS v1.2
  //   Gère l'accès à la mémoire de donnée. 
  //   reçoit la donnée contenue à cette adresse.
  //   On envoit l'adresse l'opération à besoin d'y accéder seulement, et on
  //   Ce registre et ce mux sont ici pour des raisons d'esthetique.
  //   la lecture de la mémoire de donnée en simulation plus lisible.
  //   La donnée d'écriture doit être contenu dans un registre. Cette donnée va donc
  //   de la banque de registre à la mémoire directement, sans passer par ce bloc.
  //   En effet, il permet d'éviter que toutes les instructions modifient l'adresse, ce qui rend
  //   Permet de bypassé ce bloc si on utilise pas la mémoire de donnée.
endmodule

module Memory_write_ctrl (
  input  WE,
  input  low_byte,
  input  high_byte,
  input  [15:0] Data_i,
  output LWE,
  output HWE,
  output [7:0] Low_data,
  output [7:0] High_data
);

  wire and_3_out;

  // Text text_1: pin names not known
  // Text text_2: pin names not known
  // Text text_3: pin names not known
  // Text text_4: pin names not known
  // Text text_5: pin names not known
  and and_1 (LWE, WE, low_byte);
  and and_2 (HWE, WE, high_byte);
  and and_3 (and_3_out, high_byte, low_byte);
  Multiplexer #(.width(8), .enable("false")) multiplexer_1 (
    .in0(Data_i[7:0]), .in1(Data_i[15:8]), .out(High_data), .sel(and_3_out));

  assign Low_data = Data_i[7:0];

  // Other names for the same wires on the sheet: HighByte = high_byte; LowByte = low_byte
endmodule

module Mem_Read_Ctrl (
  input  high_byte,
  input  low_byte,
  input  [7:0] low_data,
  input  [7:0] high_data,
  input  OE,
  output [15:0] data_o
);

  wire and_1_out, and_2_out, not_1_out, not_2_out;
  wire [7:0] multiplexer_1_out, multiplexer_2_out;

  // Text text_1: pin names not known
  // Text text_2: pin names not known
  // Text text_3: pin names not known
  // Text text_4: pin names not known
  // Text text_5: pin names not known
  not not_1 (not_1_out, low_byte);
  and and_1 (and_1_out, high_byte, not_1_out);
  and and_2 (and_2_out, high_byte, low_byte);
  not not_2 (not_2_out, and_2_out);
  Multiplexer #(.width(8), .enable("false")) multiplexer_1 (
    .in0(low_data), .in1(high_data), .out(multiplexer_1_out), .sel(and_1_out));
  Multiplexer #(.width(8), .enable("false")) multiplexer_2 (
    .in0(high_data), .in1({8{1'b0}}), .out(multiplexer_2_out), .sel(not_2_out));
  assign data_o = OE ? {multiplexer_2_out, multiplexer_1_out} : 16'bz;  // Controlled_Buffer controlled_buffer_1

  // Notes on the sheet:
  //   LM
  //   HM
endmodule

module ALEAS (
  input  imm,
  input  [2:0] reg_n,
  input  [2:0] reg_m,
  input  [2:0] r0,
  input  [15:0] INST,
  input  [2:0] r1,
  input  [2:0] r2,
  input  RST,
  input  CLK,
  output is_alea
);

  wire and_1_out, and_2_out, and_3_out, comparator_1_eq, comparator_2_eq, comparator_3_eq, comparator_4_eq,
       comparator_5_eq, comparator_6_eq, comparator_7_eq, comparator_8_eq, not_1_out, or_1_out, or_2_out,
       or_3_out, or_4_out;

  // Text text_1: pin names not known
  // Text text_2: pin names not known
  // Text text_3: pin names not known
  // Text text_4: pin names not known
  // Text text_5: pin names not known
  Comparator #(.width(3)) comparator_1 (.a(reg_n), .b(r0), .eq(comparator_1_eq));  // open: gt, lt
  Comparator #(.width(3)) comparator_2 (.a(reg_n), .b(r1), .eq(comparator_2_eq));  // open: gt, lt
  Comparator #(.width(3)) comparator_3 (.a(reg_n), .b(r2), .eq(comparator_3_eq));  // open: gt, lt
  Comparator #(.width(3)) comparator_4 (.a(reg_m), .b(r0), .eq(comparator_4_eq));  // open: gt, lt
  Comparator #(.width(3)) comparator_5 (.a(reg_m), .b(r1), .eq(comparator_5_eq));  // open: gt, lt
  Comparator #(.width(3)) comparator_6 (.a(reg_m), .b(r2), .eq(comparator_6_eq));  // open: gt, lt
  not not_1 (not_1_out, imm);
  or or_1 (or_1_out, comparator_1_eq, comparator_2_eq, comparator_3_eq);
  or or_2 (or_2_out, comparator_4_eq, comparator_5_eq, comparator_6_eq);
  and and_1 (and_1_out, not_1_out, or_1_out);
  and and_2 (and_2_out, not_1_out, or_2_out);
  Comparator #(.width(16)) comparator_7 (.a(INST), .b(16'h46c0), .eq(comparator_7_eq));  // open: gt, lt
  Comparator #(.width(16)) comparator_8 (.a(INST), .b({16{1'b0}}), .eq(comparator_8_eq));  // open: gt, lt
  or or_3 (or_3_out, and_1_out, and_2_out);
  or or_4 (or_4_out, comparator_7_eq, comparator_8_eq);
  Register #(.width(1)) register_1 (.D(and_3_out), .en(1'b1), .clk(CLK), .Q(is_alea), .clr(RST));
  and and_3 (and_3_out, or_3_out, ~or_4_out);  // AND_Gate
endmodule
